// Digital circuit DigLo66_Quiz1__02.dig as structural Verilog
module DigLo66_Quiz1__02 (
  input  [3:0] in0,
  input  addsubtract,
  input  [3:0] in1,
  output [2:0] out
);

  wire [2:0] add_1_s, bitcount_1_out, bitcount_2_out, sub_1_s;

  BitCount #(.Bits(4)) bitcount_1 (.in(in0), .out(bitcount_1_out));
  BitCount #(.Bits(4)) bitcount_2 (.in(in1), .out(bitcount_2_out));
  Add #(.Bits(3)) add_1 (.a(bitcount_1_out), .b(bitcount_2_out), .c_i(1'b0), .s(add_1_s));  // open: c_o
  Sub #(.Bits(3)) sub_1 (.a(bitcount_1_out), .b(bitcount_2_out), .c_i(1'b0), .s(sub_1_s));  // open: c_o
  Multiplexer #(.Bits(3)) multiplexer_1 (.sel(addsubtract), .in_0(add_1_s), .in_1(sub_1_s), .out(out));
endmodule
