// Digital circuit Quiz2_03.dig as structural Verilog
module Quiz2_03 (
  input  reset,
  input  [7:0] N,
  input  \new ,
  input  clock,
  output [7:0] num_inc,
  output [7:0] max,
  output busy
);

  wire _00, _01, _10, _11, and_1_out, and_2_out, and_3_out, gt, multiplexer_1_out, multiplexer_3_out,
       not_1_out, not_2_out, not_3_out, or_1_out, or_2_out, q1, q2;
  wire [7:0] add_1_s, multiplexer_2_out, multiplexer_4_out, multiplexer_5_out, multiplexer_6_out,
       multiplexer_7_out, val;

  Decoder #(.Selector_Bits(2)) decoder_1 (.sel({q1, q2}), .out_0(_00), .out_1(_01), .out_2(_10), .out_3(_11));
  and and_1 (and_1_out, ~reset, ~\new );  // And
  Register #(.Bits(8)) register_1 (.D(N), .C(clock), .en(\new ), .Q(val));
  Multiplexer #(.Selector_Bits(2)) multiplexer_1 (
    .sel({q1, q2}), .in_0(1'b0), .in_1(1'b1), .in_2(1'b1), .in_3(and_1_out), .out(multiplexer_1_out));
  and and_2 (and_2_out, ~reset, multiplexer_1_out);  // And
  D_FF d_ff_1 (.D(and_2_out), .C(clock), .Q(q1));  // open: nQ
  Add #(.Bits(8)) add_1 (.a(num_inc), .b(8'h1), .c_i(1'b0), .s(add_1_s));  // open: c_o
  not not_1 (not_1_out, gt);
  not not_2 (not_2_out, reset);
  Multiplexer #(.Bits(8)) multiplexer_2 (.sel(_10), .in_0(max), .in_1(val), .out(multiplexer_2_out));
  Multiplexer #(.Selector_Bits(2)) multiplexer_3 (
    .sel({q1, q2}), .in_0(\new ), .in_1(not_1_out), .in_2(1'b1), .in_3(not_2_out), .out(multiplexer_3_out));
  Multiplexer #(.Bits(8)) multiplexer_4 (.sel(_10), .in_0(max), .in_1(multiplexer_2_out), .out(multiplexer_4_out));
  Multiplexer #(.Bits(8)) multiplexer_5 (.sel(_10), .in_0(num_inc), .in_1(add_1_s), .out(multiplexer_5_out));
  and and_3 (and_3_out, ~reset, multiplexer_3_out);  // And
  Multiplexer #(.Bits(8)) multiplexer_6 (
    .sel(reset), .in_0(multiplexer_4_out), .in_1({8{1'b0}}), .out(multiplexer_6_out));
  Multiplexer #(.Bits(8)) multiplexer_7 (
    .sel(reset), .in_0(multiplexer_5_out), .in_1({8{1'b0}}), .out(multiplexer_7_out));
  or or_1 (or_1_out, reset, _10);
  D_FF d_ff_2 (.D(and_3_out), .C(clock), .Q(q2));  // open: nQ
  Register #(.Bits(8)) register_2 (.D(multiplexer_6_out), .C(clock), .en(or_1_out), .Q(max));
  Register #(.Bits(8)) register_3 (.D(multiplexer_7_out), .C(clock), .en(or_1_out), .Q(num_inc));
  or or_2 (or_2_out, _01, _10);
  Comparator #(.Bits(8)) comparator_1 (.a(val), .b(max), .gt(gt));  // open: eq, lt
  and and_4 (busy, or_2_out, not_3_out);
  not not_3 (not_3_out, reset);

  // Other names for the same wires on the sheet: clk = clock; cnt[7:0] = num_inc; mx[7:0] = max
endmodule

/* Test case T06:
N new reset clock num_inc max busy
0 0 1 0 x x x
0 0 1 1 0 0 0
131 1 0 0 x x x
131 1 0 1 x x x
0 0 0 0 x x x
0 0 0 1 x x x
0 0 0 0 x x x
0 0 0 1 x x x
0 0 0 0 x x x
0 0 0 1 x x x
0 0 0 0 x x x
0 0 0 1 x x x
0 0 0 0 x x x
0 0 0 1 x x x
0 0 0 0 x x x
0 0 0 1 x x x
0 0 0 0 x x x
0 0 0 1 x x x
0 0 0 0 x x x
0 0 0 1 x x x
0 0 0 0 x x x
0 0 0 1 x x x
0 0 0 0 x x x
0 0 0 1 x x x
0 0 0 0 x x x
0 0 0 1 x x x
0 0 0 0 x x x
0 0 0 1 x x x
0 0 0 0 x x x
0 0 0 1 x x x
0 0 0 0 x x x
0 0 0 1 x x x
0 0 0 0 x x x
0 0 0 1 x x x
0 0 0 0 x x x
0 0 0 1 x x x
0 0 0 0 x x x
0 0 0 1 x x x
0 0 0 0 x x x
0 0 0 1 x x x
0 0 0 0 x x x
0 0 0 1 x x x
0 0 0 0 x x x
0 0 0 1 x x x
0 0 0 0 x x x
0 0 0 1 x x x
0 0 0 0 x x x
0 0 0 1 x x x
0 0 0 0 x x x
0 0 0 1 x x x
0 0 0 0 x x x
0 0 0 1 x x x
0 0 0 0 x x x
0 0 0 1 x x x
0 0 0 0 x x x
0 0 0 1 x x x
0 0 0 0 x x x
0 0 0 1 x x x
0 0 0 0 x x x
0 0 0 1 x x x
0 0 0 0 x x x
0 0 0 1 x x x
0 0 0 0 x x x
0 0 0 1 x x x
0 0 0 0 1 131 0
0 0 0 1 1 131 0
130 1 0 0 x x x
130 1 0 1 x x x
0 0 0 0 x x x
0 0 0 1 x x x
0 0 0 0 x x x
0 0 0 1 x x x
0 0 0 0 x x x
0 0 0 1 x x x
0 0 0 0 x x x
0 0 0 1 x x x
0 0 0 0 x x x
0 0 0 1 x x x
0 0 0 0 x x x
0 0 0 1 x x x
0 0 0 0 x x x
0 0 0 1 x x x
0 0 0 0 x x x
0 0 0 1 x x x
0 0 0 0 x x x
0 0 0 1 x x x
0 0 0 0 x x x
0 0 0 1 x x x
0 0 0 0 x x x
0 0 0 1 x x x
0 0 0 0 x x x
0 0 0 1 x x x
0 0 0 0 x x x
0 0 0 1 x x x
0 0 0 0 x x x
0 0 0 1 x x x
0 0 0 0 x x x
0 0 0 1 x x x
0 0 0 0 x x x
0 0 0 1 x x x
0 0 0 0 x x x
0 0 0 1 x x x
0 0 0 0 x x x
0 0 0 1 x x x
0 0 0 0 x x x
0 0 0 1 x x x
0 0 0 0 x x x
0 0 0 1 x x x
0 0 0 0 x x x
0 0 0 1 x x x
0 0 0 0 x x x
0 0 0 1 x x x
0 0 0 0 x x x
0 0 0 1 x x x
0 0 0 0 x x x
0 0 0 1 x x x
0 0 0 0 x x x
0 0 0 1 x x x
0 0 0 0 x x x
0 0 0 1 x x x
0 0 0 0 x x x
0 0 0 1 x x x
0 0 0 0 x x x
0 0 0 1 x x x
0 0 0 0 x x x
0 0 0 1 x x x
0 0 0 0 x x x
0 0 0 1 x x x
0 0 0 0 1 131 0
0 0 0 1 1 131 0
58 1 0 0 x x x
58 1 0 1 x x x
0 0 0 0 x x x
0 0 0 1 x x x
0 0 0 0 x x x
0 0 0 1 x x x
0 0 0 0 x x x
0 0 0 1 x x x
0 0 0 0 x x x
0 0 0 1 x x x
0 0 0 0 x x x
0 0 0 1 x x x
0 0 0 0 x x x
0 0 0 1 x x x
0 0 0 0 x x x
0 0 0 1 x x x
0 0 0 0 x x x
0 0 0 1 x x x
0 0 0 0 x x x
0 0 0 1 x x x
0 0 0 0 x x x
0 0 0 1 x x x
0 0 0 0 x x x
0 0 0 1 x x x
0 0 0 0 x x x
0 0 0 1 x x x
0 0 0 0 x x x
0 0 0 1 x x x
0 0 0 0 x x x
0 0 0 1 x x x
0 0 0 0 x x x
0 0 0 1 x x x
0 0 0 0 x x x
0 0 0 1 x x x
0 0 0 0 x x x
0 0 0 1 x x x
0 0 0 0 x x x
0 0 0 1 x x x
0 0 0 0 x x x
0 0 0 1 x x x
0 0 0 0 x x x
0 0 0 1 x x x
0 0 0 0 x x x
0 0 0 1 x x x
0 0 0 0 x x x
0 0 0 1 x x x
0 0 0 0 x x x
0 0 0 1 x x x
0 0 0 0 x x x
0 0 0 1 x x x
0 0 0 0 x x x
0 0 0 1 x x x
0 0 0 0 x x x
0 0 0 1 x x x
0 0 0 0 x x x
0 0 0 1 x x x
0 0 0 0 x x x
0 0 0 1 x x x
0 0 0 0 x x x
0 0 0 1 x x x
0 0 0 0 x x x
0 0 0 1 x x x
0 0 0 0 1 131 0
0 0 0 1 1 131 0
154 1 0 0 x x x
154 1 0 1 x x x
0 0 0 0 x x x
0 0 0 1 x x x
0 0 0 0 x x x
0 0 0 1 x x x
0 0 0 0 x x x
0 0 0 1 x x x
0 0 0 0 x x x
0 0 0 1 x x x
0 0 0 0 x x x
0 0 0 1 x x x
0 0 0 0 x x x
0 0 0 1 x x x
0 0 0 0 x x x
0 0 0 1 x x x
0 0 0 0 x x x
0 0 0 1 x x x
0 0 0 0 x x x
0 0 0 1 x x x
0 0 0 0 x x x
0 0 0 1 x x x
0 0 0 0 x x x
0 0 0 1 x x x
0 0 0 0 x x x
0 0 0 1 x x x
0 0 0 0 x x x
0 0 0 1 x x x
0 0 0 0 x x x
0 0 0 1 x x x
0 0 0 0 x x x
0 0 0 1 x x x
0 0 0 0 x x x
0 0 0 1 x x x
0 0 0 0 x x x
0 0 0 1 x x x
0 0 0 0 x x x
0 0 0 1 x x x
0 0 0 0 x x x
0 0 0 1 x x x
0 0 0 0 x x x
0 0 0 1 x x x
0 0 0 0 x x x
0 0 0 1 x x x
0 0 0 0 x x x
0 0 0 1 x x x
0 0 0 0 x x x
0 0 0 1 x x x
0 0 0 0 x x x
0 0 0 1 x x x
0 0 0 0 x x x
0 0 0 1 x x x
0 0 0 0 x x x
0 0 0 1 x x x
0 0 0 0 x x x
0 0 0 1 x x x
0 0 0 0 x x x
0 0 0 1 x x x
0 0 0 0 x x x
0 0 0 1 x x x
0 0 0 0 x x x
0 0 0 1 x x x
0 0 0 0 2 154 0
0 0 0 1 2 154 0
122 1 0 0 x x x
122 1 0 1 x x x
0 0 0 0 x x x
0 0 0 1 x x x
0 0 0 0 x x x
0 0 0 1 x x x
0 0 0 0 x x x
0 0 0 1 x x x
0 0 0 0 x x x
0 0 0 1 x x x
0 0 0 0 x x x
0 0 0 1 x x x
0 0 0 0 x x x
0 0 0 1 x x x
0 0 0 0 x x x
0 0 0 1 x x x
0 0 0 0 x x x
0 0 0 1 x x x
0 0 0 0 x x x
0 0 0 1 x x x
0 0 0 0 x x x
0 0 0 1 x x x
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*/
