// Digital circuit DigLo68_Project_Full-6833177921-2248413.dig as structural Verilog
module DigLo68_Project_Full_6833177921_2248413 (
  input  [7:0] M,
  input  [7:0] N,
  input  [13:0] progIn,
  input  reset,
  input  progLoad,
  input  start,
  input  result,
  input  clk,
  output valid,
  output [7:0] \output ,
  output [5:0] out_11,
  output [7:0] out_12,
  output [13:0] out_13,
  output [7:0] out_14,
  output [7:0] out_15,
  output [7:0] out_16,
  output [3:0] out_17,
  output done,
  output [7:0] out_19,
  output [7:0] out_20,
  output [7:0] out_21,
  output [7:0] out_22,
  output [15:0] out_23,
  output [7:0] out_24,
  output [7:0] out_25,
  output [7:0] out_26
);

  wire _00, _0000, _0001, _01, _0010, _0100, _0101, _0110, _0111, _1000, _1001, _1010, _1011, _1100, _1101,
       _1110, _1111, a_eq__eq_b, a_gt_b, a_lt_b, accA_controller, accB_controller, and_2_out, and_3_out,
       and_4_out, and_5_out, and_6_out, and_7_out, and_9_out, and_10_out, and_11_out, and_12_out, b_a_opcode,
       comparator_1_eq, comparator_2_gt, comparator_3_gt, comparator_4_gt, comparator_6_gt, comparator_11_eq,
       comparator_12_eq, comparator_13_eq, comparator_14_eq, comparator_15_eq, comparator_16_eq,
       comparator_17_eq, comparator_21_eq, comparator_22_eq, comparator_23_eq, comparator_24_eq,
       comparator_25_eq, comparator_26_eq, comparator_27_eq, comparator_28_eq, comparator_29_eq,
       comparator_30_eq, comparator_31_eq, comparator_32_eq, comparator_33_eq, comparator_34_eq, eq,
       eqController, gt, gtController, i_2_lt__eq_accB, i_f1_lt_target, isFuture1, isFuture2, isHALT, isLCM,
       isPrime_d, isPrimeOpcode, jumpController, lt, ltController, multiplexer_5_out, multiplexer_26_out,
       multiplexer_29_out, multiplexer_30_out, multiplexer_31_out, multiplexer_32_out, multiplexer_33_out,
       multiplexer_38_out, multiplexer_39_out, multiplexer_40_out, multiplexer_41_out, multiplexer_42_out,
       multiplexer_43_out, multiplexer_44_out, multiplexer_45_out, nand_1_out, nand_2_out, nand_3_out,
       nand_4_out, nand_5_out, not_1_out, not_2_out, not_3_out, not_6_out, not_8_out, not_9_out, not_10_out,
       not_11_out, or_1_out, or_2_out, or_3_out, or_4_out, or_5_out, or_6_out, or_7_out, or_8_out, or_9_out,
       or_10_out, or_11_out, or_12_out, or_13_out, or_22_out, or_23_out, or_24_out, Q, regC_controller,
       regD_controller, rRAM_iter_lt_16;
  wire [2:0] add_1_s, i_f1, multiplexer_20_out, target;
  wire [3:0] rom_1_d;
  wire [7:0] _1A, _2A, a, add_2_s, \and , clear_iter, div_2_r, minus, multiplexer_1_out, multiplexer_2_out,
       multiplexer_3_out, multiplexer_4_out, multiplexer_6_out, multiplexer_7_out, multiplexer_8_out,
       multiplexer_11_out, multiplexer_12_out, multiplexer_13_out, multiplexer_14_out, multiplexer_15_out,
       multiplexer_16_out, multiplexer_17_out, multiplexer_22_out, multiplexer_23_out, multiplexer_27_out,
       multiplexer_28_out, multiplexer_34_out, multiplexer_35_out, multiplexer_36_out, multiplexer_37_out,
       multiplexer_46_out, multiplexer_47_out, multiplexer_48_out, multiplexer_49_out, multiplexer_50_out,
       multiplexer_51_out, multiplexer_55_out, multiplexer_56_out, multiplexer_57_out, multiply, newA, newB,
       newC, newD, \or , pow, pRAM_counter, quotient, remain, rotateShiftLeft, rotateShiftRight, rRAM_Oprand,
       rRAM_oprand_3__0, shiftLeft, shiftRight, sum, \xor ;
  wire [13:8] pRAM_d2;
  wire [15:0] lcm, mn, multiplexer_24_out, multiplexer_25_out;
  wire [31:0] mul_1_mul;

  Multiplexer #(.Bits(8)) multiplexer_1 (.sel(_1110), .in_0(out_12), .in_1(8'h9), .out(multiplexer_1_out));
  Multiplexer #(.Bits(8)) multiplexer_2 (.sel(_1011), .in_0(multiplexer_1_out), .in_1(8'hb), .out(multiplexer_2_out));
  Multiplexer #(.Bits(8)) multiplexer_3 (.sel(_1010), .in_0(multiplexer_2_out), .in_1(8'ha), .out(multiplexer_3_out));
  Multiplexer #(.Bits(8)) multiplexer_4 (.sel(_0101), .in_0(multiplexer_3_out), .in_1(8'hf), .out(multiplexer_4_out));
  Multiplexer multiplexer_5 (.sel(reset), .in_0(isHALT), .in_1(1'b0), .out(multiplexer_5_out));
  or or_1 (or_1_out, _0111, reset);
  or or_2 (or_2_out, progLoad, result, reset);
  Multiplexer #(.Bits(8)) multiplexer_6 (.sel(_0100), .in_0(multiplexer_4_out), .in_1(8'he), .out(multiplexer_6_out));
  Register register_1 (.D(multiplexer_5_out), .C(clk), .en(or_1_out), .Q(valid));
  and and_1 (done, not_1_out, not_2_out);
  not not_1 (not_1_out, rRAM_iter_lt_16);
  not not_2 (not_2_out, or_2_out);
  not not_3 (not_3_out, progLoad);
  or or_3 (or_3_out, _0000, _0110);
  Counter #(.Bits(8)) counter_1 (.en(progLoad), .C(clk), .clr(not_3_out), .out(pRAM_counter));  // open: ovf
  CounterPreset #(.Bits(8)) counterpreset_1 (
    .en(or_3_out), .C(clk), .dir(1'b0), .in(out_12), .ld(jumpController), .clr(_0000), .out(out_20));  // open: ovf
  Multiplexer #(.Bits(8)) multiplexer_7 (.sel(_1011), .in_0(out_23[15:8]), .in_1(out_23[7:0]), .out(multiplexer_7_out));
  and and_2 (and_2_out, isLCM, _0010);
  Multiplexer #(.Bits(8)) multiplexer_8 (
    .sel(isFuture1), .in_0(out_16), .in_1(multiplexer_7_out), .out(multiplexer_8_out));
  Multiplexer #(.Bits(8)) multiplexer_9 (
    .sel(and_2_out), .in_0(multiplexer_6_out), .in_1({4'b0000, out_12[7:4]}), .out(_1A));
  Multiplexer #(.Bits(8)) multiplexer_10 (.sel(and_2_out), .in_0(out_19), .in_1({4'b0000, out_12[3:0]}), .out(_2A));
  Seven_Seg_Hex seven_seg_hex_1 (.d(out_22[7:4]), .dp(1'b0));
  Multiplexer #(.Bits(8)) multiplexer_11 (.sel(progLoad), .in_0(out_20), .in_1(pRAM_counter), .out(multiplexer_11_out));
  Seven_Seg_Hex seven_seg_hex_2 (.d(out_22[3:0]), .dp(1'b0));
  Multiplexer #(.Bits(8)) multiplexer_12 (
    .sel(_1110), .in_0(multiplexer_8_out), .in_1(out_24), .out(multiplexer_12_out));
  Comparator #(.Bits(6)) comparator_1 (.a(out_11), .b(6'b010001), .eq(comparator_1_eq));  // open: gt, lt
  Multiplexer #(.Bits(8)) multiplexer_13 (.sel(_0101), .in_0(lcm[15:8]), .in_1(lcm[7:0]), .out(multiplexer_13_out));
  RAMDualAccess #(.AddrBits(8), .Bits(14)) pRAM (
    .str(progLoad), .C(clk), .ld(1'b1), .A1(multiplexer_11_out), .Din1(progIn), .A2(multiplexer_14_out),
    .D1(out_13), .D2({pRAM_d2, out_25}));
  Multiplexer #(.Bits(8)) multiplexer_14 (.sel(isFuture2), .in_0(out_12), .in_1(out_26), .out(multiplexer_14_out));
  Multiplexer #(.Bits(8)) multiplexer_15 (
    .sel(isLCM), .in_0(multiplexer_12_out), .in_1(multiplexer_13_out), .out(multiplexer_15_out));
  or or_4 (or_4_out, _0100, _0101, comparator_1_eq, _1010, _1011, _1110, _01);
  Multiplexer #(.Bits(8)) multiplexer_16 (
    .sel(_01), .in_0(multiplexer_15_out), .in_1({8{1'b0}}), .out(multiplexer_16_out));
  Register #(.Bits(3)) register_2 (.D(out_16[2:0]), .C(clk), .en(_0010), .Q(target));
  Multiplexer #(.Bits(8)) multiplexer_17 (.sel(_01), .in_0(_1A), .in_1(clear_iter), .out(multiplexer_17_out));
  Multiplexer #(.Bits(6)) multiplexer_18 (.sel(_0000), .in_0(out_13[13:8]), .in_1({6{1'b0}}), .out(out_11));
  Multiplexer #(.Bits(8)) multiplexer_19 (.sel(_0000), .in_0(out_13[7:0]), .in_1({8{1'b0}}), .out(out_12));
  RAMDualAccess #(.AddrBits(8), .Bits(8)) rRAM (
    .str(or_4_out), .C(clk), .ld(1'b1), .A1(multiplexer_17_out), .Din1(multiplexer_16_out), .A2(_2A),
    .D1(rRAM_Oprand), .D2(rRAM_oprand_3__0));
  Add #(.Bits(3)) add_1 (.a(i_f1), .b(3'b001), .c_i(1'b0), .s(add_1_s));  // open: c_o
  Multiplexer #(.Bits(3)) multiplexer_20 (.sel(_0010), .in_0(add_1_s), .in_1(3'b001), .out(multiplexer_20_out));
  or or_5 (or_5_out, _0010, _1001);
  Mul #(.Bits(16)) mul_1 (.a(out_23), .b({{13{1'b0}}, i_f1}), .mul(mul_1_mul));
  Multiplexer #(.Bits(8)) multiplexer_21 (
    .sel(rRAM_iter_lt_16), .in_0({8{1'b0}}), .in_1(rRAM_oprand_3__0), .out(out_22));
  Register #(.Bits(3)) register_3 (.D(multiplexer_20_out), .C(clk), .en(or_5_out), .Q(i_f1));
  Comparator #(.Signed("true"), .Bits(8)) comparator_2 (.a(out_25), .b(out_24), .gt(comparator_2_gt));  // open: eq, lt
  Add #(.Bits(8)) add_2 (.a(out_26), .b(8'h1), .c_i(1'b0), .s(add_2_s));  // open: c_o
  Comparator #(.Bits(8)) comparator_3 (.a(out_26), .b(out_15), .gt(comparator_3_gt));  // open: eq, lt
  Comparator #(.Bits(3)) comparator_4 (.a(i_f1), .b(target), .gt(comparator_4_gt));  // open: eq, lt
  not not_4 (i_f1_lt_target, comparator_4_gt);
  or or_6 (or_6_out, _0010, _1100);
  or or_7 (or_7_out, _0010, _1100, _1101);
  not not_5 (i_2_lt__eq_accB, comparator_3_gt);
  Counter #(.Bits(8)) counter_2 (.en(_01), .C(clk), .clr(_00), .out(clear_iter));  // open: ovf
  Multiplexer #(.Bits(8)) multiplexer_22 (.sel(or_6_out), .in_0(add_2_s), .in_1(out_16), .out(multiplexer_22_out));
  or or_8 (or_8_out, progLoad, result, reset);
  Multiplexer #(.Bits(8)) multiplexer_23 (
    .sel(comparator_2_gt), .in_0(out_24), .in_1(out_25), .out(multiplexer_23_out));
  Register #(.Bits(8)) register_4 (.D(multiplexer_22_out), .C(clk), .en(or_7_out), .Q(out_26));
  Multiplexer #(.Bits(16)) multiplexer_24 (
    .sel(i_f1_lt_target), .in_0(out_23), .in_1(mul_1_mul[15:0]), .out(multiplexer_24_out));
  Comparator #(.Bits(8)) comparator_5 (.a(out_19), .b(8'h10), .lt(rRAM_iter_lt_16));  // open: gt, eq
  Counter #(.Bits(8)) counter_3 (.en(_0001), .C(clk), .clr(or_8_out), .out(out_19));  // open: ovf
  Comparator #(.Bits(8)) comparator_6 (.a(clear_iter), .b(8'h10), .gt(comparator_6_gt));  // open: eq, lt
  Multiplexer #(.Bits(16)) multiplexer_25 (
    .sel(_0010), .in_0(multiplexer_24_out), .in_1(16'h1), .out(multiplexer_25_out));
  Multiplexer multiplexer_26 (.sel(Q), .in_0(reset), .in_1(comparator_6_gt), .out(multiplexer_26_out));
  or or_9 (or_9_out, _0010, _1000);
  D_FF d_ff_1 (.D(multiplexer_26_out), .C(clk), .Q(Q));  // open: nQ
  Decoder decoder_1 (.sel(Q), .out_0(_00), .out_1(_01));
  Multiplexer #(.Bits(8)) multiplexer_27 (
    .sel(_1100), .in_0(multiplexer_23_out), .in_1(out_25), .out(multiplexer_27_out));
  Register #(.Bits(16)) register_5 (.D(multiplexer_25_out), .C(clk), .en(or_9_out), .Q(out_23));
  or or_10 (or_10_out, _0010, _1100, _1111);
  Multiplexer #(.Bits(8)) multiplexer_28 (
    .sel(_0010), .in_0(multiplexer_27_out), .in_1({8{1'b0}}), .out(multiplexer_28_out));
  Register #(.Bits(8)) register_6 (.D(multiplexer_28_out), .C(clk), .en(or_10_out), .Q(out_24));
  Comparator #(.Bits(6)) comparator_7 (.a(out_11), .b(6'b110011), .eq(isLCM));  // open: gt, lt
  Comparator #(.Bits(6)) comparator_8 (.a(out_11), .b({6{1'b1}}), .eq(isHALT));  // open: gt, lt
  Comparator #(.Bits(6)) comparator_9 (.a(out_11), .b(6'b110100), .eq(isFuture1));  // open: gt, lt
  Comparator #(.Bits(6)) comparator_10 (.a(out_11), .b(6'b110101), .eq(isFuture2));  // open: gt, lt
  or or_11 (or_11_out, isFuture1, isFuture2);
  ROM #(.AddrBits(6), .Bits(4)) rom_1 (.A(out_11), .sel(1'b1), .D(rom_1_d));
  or or_12 (or_12_out, eq, lt);
  or or_13 (or_13_out, eq, gt);
  Comparator #(.Bits(6)) comparator_11 (.a(out_11), .b(6'b010111), .eq(comparator_11_eq));  // open: gt, lt
  Comparator #(.Bits(6)) comparator_12 (.a(out_11), .b(6'b010110), .eq(comparator_12_eq));  // open: gt, lt
  Comparator #(.Bits(6)) comparator_13 (.a(out_11), .b(6'b010101), .eq(comparator_13_eq));  // open: gt, lt
  Comparator #(.Bits(6)) comparator_14 (.a(out_11), .b(6'b010100), .eq(comparator_14_eq));  // open: gt, lt
  Comparator #(.Bits(6)) comparator_15 (.a(out_11), .b(6'b010011), .eq(comparator_15_eq));  // open: gt, lt
  Comparator #(.Bits(6)) comparator_16 (.a(out_11), .b(6'b010010), .eq(comparator_16_eq));  // open: gt, lt
  Comparator #(.Bits(6)) comparator_17 (.a(out_11), .b(6'b110000), .eq(comparator_17_eq));  // open: gt, lt
  Comparator #(.Bits(6)) comparator_18 (.a(out_11), .b(6'b110001), .eq(isPrimeOpcode));  // open: gt, lt
  Comparator #(.Bits(6)) comparator_19 (.a(out_11), .b(6'b110010), .eq(b_a_opcode));  // open: gt, lt
  Add #(.Bits(8)) add_3 (.a(out_16), .b(out_15), .c_i(1'b0), .s(sum));  // open: c_o
  Sub #(.Bits(8)) sub_1 (.a(out_16), .b(out_15), .c_i(1'b0), .s(minus));  // open: c_o
  Mul #(.Bits(4)) mul_2 (.a(out_16[3:0]), .b(out_15[3:0]), .mul(multiply));
  Div #(.Bits(8)) div_1 (.a(out_16), .b(out_15), .q(quotient), .r(remain));
  Multiplexer #(.Selector_Bits(4)) multiplexer_29 (
    .sel(out_17), .in_0(1'b0), .in_1(1'b0), .in_2(or_11_out), .in_3(1'b0), .in_4(1'b0), .in_5(1'b0),
    .in_6(1'b0), .in_7(1'b0), .in_8(1'b1), .in_9(1'b1), .in_10(1'b1), .in_11(1'b0), .in_12(1'b1),
    .in_13(1'b1), .in_14(1'b0), .in_15(1'b1), .out(multiplexer_29_out));
  nand nand_1 (nand_1_out, comparator_11_eq, or_12_out);
  nand nand_2 (nand_2_out, comparator_12_eq, or_13_out);
  nand nand_3 (nand_3_out, comparator_13_eq, lt);
  nand nand_4 (nand_4_out, comparator_14_eq, gt);
  nand nand_5 (nand_5_out, comparator_15_eq, eq);
  and and_3 (and_3_out, multiplexer_29_out, not_6_out);
  not not_6 (not_6_out, reset);
  and and_4 (and_4_out, rom_1_d[3], _0110);
  and and_5 (and_5_out, rom_1_d[2], _0110);
  and and_6 (and_6_out, rom_1_d[1], _0110);
  and and_7 (and_7_out, rom_1_d[0], _0110);
  nand nand_6 (jumpController, nand_1_out, nand_2_out, nand_3_out, nand_4_out, nand_5_out, ~comparator_16_eq);  // NAnd
  or or_14 (gtController, comparator_17_eq, reset);
  or or_15 (ltController, comparator_17_eq, reset);
  or or_16 (eqController, comparator_17_eq, isPrimeOpcode, b_a_opcode, reset);
  assign \and  = out_16 & out_15;  // And and_8, 8 bits wide
  assign \or  = out_16 | out_15;  // Or or_17, 8 bits wide
  assign \xor  = out_16 ^ out_15;  // XOr xor_1, 8 bits wide
  D_FF d_ff_2 (.D(and_3_out), .C(clk), .Q(out_17[3]));  // open: nQ
  assign a = ~out_16;  // Not not_7, 8 bits wide
  Multiplexer multiplexer_30 (.sel(isFuture2), .in_0(1'b1), .in_1(1'b1), .out(multiplexer_30_out));
  or or_18 (accA_controller, and_4_out, reset);
  or or_19 (accB_controller, and_5_out, reset);
  or or_20 (regC_controller, and_6_out, reset);
  or or_21 (regD_controller, and_7_out, reset);
  Multiplexer multiplexer_31 (.sel(isFuture1), .in_0(multiplexer_30_out), .in_1(1'b0), .out(multiplexer_31_out));
  Multiplexer #(.Selector_Bits(4)) multiplexer_32 (
    .sel(out_17), .in_0(1'b0), .in_1(1'b0), .in_2(multiplexer_31_out), .in_3(1'b0), .in_4(1'b1), .in_5(1'b1),
    .in_6(1'b0), .in_7(1'b0), .in_8(1'b0), .in_9(1'b0), .in_10(1'b0), .in_11(1'b1), .in_12(1'b1),
    .in_13(1'b1), .in_14(1'b1), .in_15(1'b1), .out(multiplexer_32_out));
  BarrelShifter #(.Bits(8)) barrelshifter_1 (.in(out_16), .shift({1'b0, out_15[2:0]}), .out(shiftLeft));
  BarrelShifter #(.Bits(8), .direction("right")) barrelshifter_2 (
    .in(out_16), .shift({1'b0, out_15[2:0]}), .out(shiftRight));
  BarrelShifter #(.Bits(8), .barrelShifterMode("rotate")) barrelshifter_3 (
    .in(out_16), .shift({1'b0, out_15[2:0]}), .out(rotateShiftLeft));
  BarrelShifter #(.Bits(8), .barrelShifterMode("rotate"), .direction("right")) barrelshifter_4 (
    .in(out_16), .shift({1'b0, out_15[2:0]}), .out(rotateShiftRight));
  or or_22 (or_22_out, ~isLCM, isHALT);  // Or
  and and_9 (and_9_out, multiplexer_32_out, not_8_out);
  not not_8 (not_8_out, reset);
  Comparator #(.Signed("true"), .Bits(8)) comparator_20 (
    .a(out_16), .b(out_15), .gt(a_gt_b), .eq(a_eq__eq_b), .lt(a_lt_b));
  ROM #(.AddrBits(8)) isPrime (.A(out_16), .sel(1'b1), .D(isPrime_d));
  Multiplexer multiplexer_33 (.sel(isFuture2), .in_0(or_22_out), .in_1(1'b0), .out(multiplexer_33_out));
  D_FF d_ff_3 (.D(and_9_out), .C(clk), .Q(out_17[2]));  // open: nQ
  Multiplexer #(.Bits(8)) multiplexer_34 (.sel(reset), .in_0(newA), .in_1({8{1'b0}}), .out(multiplexer_34_out));
  Multiplexer #(.Bits(8)) multiplexer_35 (.sel(reset), .in_0(newB), .in_1({8{1'b0}}), .out(multiplexer_35_out));
  Multiplexer #(.Bits(8)) multiplexer_36 (.sel(reset), .in_0(newC), .in_1({8{1'b0}}), .out(multiplexer_36_out));
  Multiplexer #(.Bits(8)) multiplexer_37 (.sel(reset), .in_0(newD), .in_1({8{1'b0}}), .out(multiplexer_37_out));
  Multiplexer multiplexer_38 (.sel(isFuture1), .in_0(multiplexer_33_out), .in_1(1'b0), .out(multiplexer_38_out));
  Multiplexer multiplexer_39 (.sel(isPrimeOpcode), .in_0(a_eq__eq_b), .in_1(isPrime_d), .out(multiplexer_39_out));
  not not_9 (not_9_out, i_f1_lt_target);
  Register #(.Bits(8)) register_7 (.D(multiplexer_34_out), .C(clk), .en(accA_controller), .Q(out_16));
  Register #(.Bits(8)) register_8 (.D(multiplexer_35_out), .C(clk), .en(accB_controller), .Q(out_15));
  Register #(.Bits(8)) register_9 (.D(multiplexer_36_out), .C(clk), .en(regC_controller), .Q(out_14));
  Register #(.Bits(8)) register_10 (.D(multiplexer_37_out), .C(clk), .en(regD_controller), .Q(out_21));
  Div #(.Bits(8)) div_2 (.a(out_16), .b(out_15), .r(div_2_r));  // open: q
  Multiplexer #(.Selector_Bits(4)) multiplexer_40 (
    .sel(out_17), .in_0(start), .in_1(1'b0), .in_2(multiplexer_38_out), .in_3(1'b0), .in_4(1'b0),
    .in_5(1'b1), .in_6(1'b1), .in_7(1'b0), .in_8(not_9_out), .in_9(1'b0), .in_10(1'b1), .in_11(1'b1),
    .in_12(1'b0), .in_13(1'b1), .in_14(1'b1), .in_15(1'b0), .out(multiplexer_40_out));
  not not_10 (not_10_out, reset);
  Comparator #(.Bits(8)) comparator_21 (.a(div_2_r), .b({8{1'b0}}), .eq(comparator_21_eq));  // open: gt, lt
  and and_10 (and_10_out, multiplexer_40_out, not_10_out);
  Multiplexer multiplexer_41 (
    .sel(b_a_opcode), .in_0(multiplexer_39_out), .in_1(comparator_21_eq), .out(multiplexer_41_out));
  Register #(.Bits(16)) register_11 (.D({rRAM_Oprand, rRAM_oprand_3__0}), .C(clk), .en(_0010), .Q(mn));
  D_FF d_ff_4 (.D(and_10_out), .C(clk), .Q(out_17[1]));  // open: nQ
  Multiplexer multiplexer_42 (.sel(reset), .in_0(a_gt_b), .in_1(1'b0), .out(multiplexer_42_out));
  Multiplexer multiplexer_43 (.sel(reset), .in_0(multiplexer_41_out), .in_1(1'b0), .out(multiplexer_43_out));
  Multiplexer multiplexer_44 (.sel(reset), .in_0(a_lt_b), .in_1(1'b0), .out(multiplexer_44_out));
  ROM #(.AddrBits(6), .Bits(8)) rom_2 (.A({out_16[2:0], out_15[2:0]}), .sel(1'b1), .D(pow));
  ROM #(.AddrBits(16), .Bits(16)) rom_3 (.A(mn), .sel(1'b1), .D(lcm));
  Register register_12 (.D(multiplexer_42_out), .C(clk), .en(gtController), .Q(gt));
  Register register_13 (.D(multiplexer_43_out), .C(clk), .en(eqController), .Q(eq));
  Register register_14 (.D(multiplexer_44_out), .C(clk), .en(ltController), .Q(lt));
  Multiplexer #(.Selector_Bits(4)) multiplexer_45 (
    .sel(out_17), .in_0(result), .in_1(rRAM_iter_lt_16), .in_2(isHALT), .in_3(1'b0), .in_4(1'b1),
    .in_5(1'b0), .in_6(1'b0), .in_7(1'b0), .in_8(i_f1_lt_target), .in_9(1'b0), .in_10(1'b1), .in_11(1'b0),
    .in_12(1'b1), .in_13(i_2_lt__eq_accB), .in_14(1'b0), .in_15(1'b1), .out(multiplexer_45_out));
  and and_11 (and_11_out, multiplexer_45_out, not_11_out);
  not not_11 (not_11_out, reset);
  D_FF d_ff_5 (.D(and_11_out), .C(clk), .Q(out_17[0]));  // open: nQ
  Comparator #(.Bits(6)) comparator_22 (.a(out_11), .b(6'b000001), .eq(comparator_22_eq));  // open: gt, lt
  Comparator #(.Bits(6)) comparator_23 (.a(out_11), .b(6'b000011), .eq(comparator_23_eq));  // open: gt, lt
  Comparator #(.Bits(6)) comparator_24 (.a(out_11), .b(6'b000110), .eq(comparator_24_eq));  // open: gt, lt
  Comparator #(.Bits(6)) comparator_25 (.a(out_11), .b(6'b001110), .eq(comparator_25_eq));  // open: gt, lt
  Comparator #(.Bits(6)) comparator_26 (.a(out_11), .b(6'b001000), .eq(comparator_26_eq));  // open: gt, lt
  Comparator #(.Bits(6)) comparator_27 (.a(out_11), .b(6'b001111), .eq(comparator_27_eq));  // open: gt, lt
  Multiplexer #(.Bits(8)) multiplexer_46 (.sel(or_23_out), .in_0(out_16), .in_1(M), .out(multiplexer_46_out));
  or or_23 (or_23_out, comparator_28_eq, comparator_31_eq);
  Comparator #(.Bits(6)) comparator_28 (.a(out_11), .b(6'b001001), .eq(comparator_28_eq));  // open: gt, lt
  Multiplexer #(.Bits(8)) multiplexer_47 (.sel(comparator_29_eq), .in_0(N), .in_1(M), .out(multiplexer_47_out));
  Comparator #(.Bits(6)) comparator_29 (.a(out_11), .b(6'b001011), .eq(comparator_29_eq));  // open: gt, lt
  Decoder #(.Selector_Bits(4)) decoder_2 (
    .sel(out_17), .out_0(_0000), .out_1(_0001), .out_2(_0010), .out_4(_0100), .out_5(_0101), .out_6(_0110),
    .out_7(_0111), .out_8(_1000), .out_9(_1001), .out_10(_1010), .out_11(_1011), .out_12(_1100),
    .out_13(_1101), .out_14(_1110), .out_15(_1111));  // open: out_3
  or or_24 (or_24_out, comparator_24_eq, comparator_25_eq);
  Multiplexer #(.Bits(8)) multiplexer_48 (
    .sel(comparator_27_eq), .in_0(rRAM_Oprand), .in_1(out_25), .out(multiplexer_48_out));
  Multiplexer #(.Bits(8)) multiplexer_49 (
    .sel(comparator_30_eq), .in_0(out_21), .in_1(out_16), .out(multiplexer_49_out));
  Comparator #(.Bits(6)) comparator_30 (.a(out_11), .b(6'b000100), .eq(comparator_30_eq));  // open: gt, lt
  Comparator #(.Bits(6)) comparator_31 (.a(out_11), .b(6'b001101), .eq(comparator_31_eq));  // open: gt, lt
  Multiplexer #(.Bits(8)) multiplexer_50 (
    .sel(comparator_26_eq), .in_0(multiplexer_48_out), .in_1(out_21), .out(multiplexer_50_out));
  Multiplexer #(.Bits(8)) multiplexer_51 (
    .sel(or_24_out), .in_0(multiplexer_50_out), .in_1(out_14), .out(multiplexer_51_out));
  Multiplexer #(.Bits(8)) multiplexer_52 (.sel(comparator_32_eq), .in_0(multiplexer_49_out), .in_1(out_12), .out(newB));
  Comparator #(.Bits(6)) comparator_32 (.a(out_11), .b(6'b000010), .eq(comparator_32_eq));  // open: gt, lt
  Multiplexer #(.Bits(8)) multiplexer_53 (.sel(comparator_33_eq), .in_0(multiplexer_46_out), .in_1(N), .out(newC));
  Comparator #(.Bits(6)) comparator_33 (.a(out_11), .b(6'b001010), .eq(comparator_33_eq));  // open: gt, lt
  Multiplexer #(.Bits(8)) multiplexer_54 (.sel(comparator_34_eq), .in_0(multiplexer_47_out), .in_1(out_16), .out(newD));
  Comparator #(.Bits(6)) comparator_34 (.a(out_11), .b(6'b000111), .eq(comparator_34_eq));  // open: gt, lt
  Multiplexer #(.Bits(8)) multiplexer_55 (
    .sel(comparator_23_eq), .in_0(multiplexer_51_out), .in_1(out_15), .out(multiplexer_55_out));
  Multiplexer #(.Selector_Bits(4), .Bits(8)) multiplexer_56 (
    .sel(out_11[3:0]), .in_0(sum), .in_1(minus), .in_2(multiply), .in_3(quotient), .in_4(remain), .in_5(pow),
    .in_6(out_16), .in_7(out_16), .in_8(a), .in_9(\and ), .in_10(\or ), .in_11(\xor ), .in_12(shiftLeft),
    .in_13(rotateShiftLeft), .in_14(shiftRight), .in_15(rotateShiftRight), .out(multiplexer_56_out));
  Multiplexer #(.Bits(8)) multiplexer_57 (
    .sel(comparator_22_eq), .in_0(multiplexer_55_out), .in_1(out_12), .out(multiplexer_57_out));
  Multiplexer #(.Bits(8)) multiplexer_58 (
    .sel(and_12_out), .in_0(multiplexer_57_out), .in_1(multiplexer_56_out), .out(newA));
  and and_12 (and_12_out, out_11[5], ~out_11[4]);  // And

  assign \output  = out_22;

  // Other names for the same wires on the sheet: pRAM_adr_Oprand[7:0] = out_25; pRAM_i_2__7__0[7:0] = out_25;
  //   accA[7:0] = out_16; accB[7:0] = out_15; Fac[15:0] = out_23; i_f2[7:0] = out_26; max[7:0] = out_24;
  //   opcode[5:0] = out_11; operand[7:0] = out_12; PC[7:0] = out_20; pIN[13:0] = progIn; Q1 = out_17[3];
  //   Q2 = out_17[2]; Q3 = out_17[1]; Q4 = out_17[0]; regC[7:0] = out_14; regD[7:0] = out_21; res = result;
  //   rRAM_iter[7:0] = out_19; rRAM_oprand_7__4[7:0] = rRAM_Oprand; st = start

  // Notes on the sheet:
  //   แก้อยู่
  //   rRAM
  //   Address Choosing
  //   Outputs
  //   pRAM
  //   pRAM Counter
  //   pRAM Accessing
  //   rRAM Storing and Accessing
  //   rRAM Iterator
  //   clear_iter
  //   เสร็จแล้ว
  //   Testcases 68
  //   Variables
  //   Inputs
  //   Loggings
  //   accA, accB, regC, regD 's controllers
  //   Jump's Controller
  //   Flags' Controller
  //   Operators
  //   Cur State -> Next State
  //   contents of rom_1 (hex, n*v repeats v):
  //   0,8,4,8,4,2,8,1,8,2,2,1,1,3,c,8,8,15*0,6*8,0,0,8*8
  //   Flags Variable
  //   accA, accB, regC, regD Variables
  //   contents of isPrime (hex, n*v repeats v):
  //   0,0,1,1,0,1,0,1,0,0,0,1,0,1,0,0,0,1,0,1,0,0,0,1,5*0,1,0,1,5*0
  //   ,1,0,0,0,1,0,1,0,0,0,1,5*0,1,5*0,1,0,1,5*0,1,0,0,0,1,0,1,5*0,1
  //   ,0,0,0,1,5*0,1,7*0,1,0,0,0,1,0,1,0,0,0,1,0,1,0,0,0,1,13*0,1,0,0,0
  //   ,1,5*0,1,0,1,9*0,1,0,1,5*0,1,5*0,1,0,0,0,1,5*0,1,5*0,1,0,1,9*0
  //   ,1,0,1,0,0,0,1,0,1,11*0,1,11*0,1,0,0,0,1,0,1,0,0,0,1,5*0,1,0,1
  //   ,9*0,1
  //   LCM
  //   contents of rom_2 (hex, n*v repeats v):
  //   1,7*0,9*1,2,4,8,10,20,40,80,1,3,9,1b,51,f3,d9,8b,1,4,10,40,4*0
  //   ,1,5,19,7d,71,35,9,2d,1,6,24,d8,10,60,40,80,1,7,31,57,61,a7,91,f7
  //   contents of rom_3 (hex, n*v repeats v):
  //   257*0,1,2,3,4,5,6,7,8,9,a,b,c,d,e,f,10,11,12,13,14,15,16,17,18
  //   ,19,1a,1b,1c,1d,1e,1f,20,21,22,23,24,25,26,27,28,29,2a,2b,2c,2d
  //   ,2e,2f,30,31,32,33,34,35,36,37,38,39,3a,3b,3c,3d,3e,3f,40,41,42
  //   ,43,44,45,46,47,48,49,4a,4b,4c,4d,4e,4f,50,51,52,53,54,55,56,57
  //   ,58,59,5a,5b,5c,5d,5e,5f,60,61,62,63,64,65,66,67,68,69,6a,6b,6c
  //   ,6d,6e,6f,70,71,72,73,74,75,76,77,78,79,7a,7b,7c,7d,7e,7f,80,81
  //   ,82,83,84,85,86,87,88,89,8a,8b,8c,8d,8e,8f,90,91,92,93,94,95,96
  //   ,97,98,99,9a,9b,9c,9d,9e,9f,a0,a1,a2,a3,a4,a5,a6,a7,a8,a9,aa,ab
  //   ,ac,ad,ae,af,b0,b1,b2,b3,b4,b5,b6,b7,b8,b9,ba,bb,bc,bd,be,bf,c0
  //   ,c1,c2,c3,c4,c5,c6,c7,c8,c9,ca,cb,cc,cd,ce,cf,d0,d1,d2,d3,d4,d5
  //   ,d6,d7,d8,d9,da,db,dc,dd,de,df,e0,e1,e2,e3,e4,e5,e6,e7,e8,e9,ea
  //   ,eb,ec,ed,ee,ef,f0,f1,f2,f3,f4,f5,f6,f7,f8,f9,fa,fb,fc,fd,fe,ff
  //   ,0,2,2,6,4,a,6,e,8,12,a,16,c,1a,e,1e,10,22,12,26,14,2a,16,2e,18
  //   ,32,1a,36,1c,3a,1e,3e,20,42,22,46,24,4a,26,4e,28,52,2a,56,2c,5a
  //   ,2e,5e,30,62,32,66,34,6a,36,6e,38,72,3a,76,3c,7a,3e,7e,40,82,42
  //   ,86,44,8a,46,8e,48,92,4a,96,4c,9a,4e,9e,50,a2,52,a6,54,aa,56,ae
  //   ,58,b2,5a,b6,5c,ba,5e,be,60,c2,62,c6,64,ca,66,ce,68,d2,6a,d6,6c
  //   ,da,6e,de,70,e2,72,e6,74,ea,76,ee,78,f2,7a,f6,7c,fa,7e,fe,80,102
  //   ,82,106,84,10a,86,10e,88,112,8a,116,8c,11a,8e,11e,90,122,92,126
  //   ,94,12a,96,12e,98,132,9a,136,9c,13a,9e,13e,a0,142,a2,146,a4,14a
  //   ,a6,14e,a8,152,aa,156,ac,15a,ae,15e,b0,162,b2,166,b4,16a,b6,16e
  //   ,b8,172,ba,176,bc,17a,be,17e,c0,182,c2,186,c4,18a,c6,18e,c8,192
  //   ,ca,196,cc,19a,ce,19e,d0,1a2,d2,1a6,d4,1aa,d6,1ae,d8,1b2,da,1b6
  //   ,dc,1ba,de,1be,e0,1c2,e2,1c6,e4,1ca,e6,1ce,e8,1d2,ea,1d6,ec,1da
  //   ,ee,1de,f0,1e2,f2,1e6,f4,1ea,f6,1ee,f8,1f2,fa,1f6,fc,1fa,fe,1fe
  //   ,0,3,6,3,c,f,6,15,18,9,1e,21,c,27,2a,f,30,33,12,39,3c,15,42,45
  //   ,18,4b,4e,1b,54,57,1e,5d,60,21,66,69,24,6f,72,27,78,7b,2a,81,84
  //   ,2d,8a,8d,30,93,96,33,9c,9f,36,a5,a8,39,ae,b1,3c,b7,ba,3f,c0,c3
  //   ,42,c9,cc,45,d2,d5,48,db,de,4b,e4,e7,4e,ed,f0,51,f6,f9,54,ff,102
  //   ,57,108,10b,5a,111,114,5d,11a,11d,60,123,126,63,12c,12f,66,135
  //   ,138,69,13e,141,6c,147,14a,6f,150,153,72,159,15c,75,162,165,78
  //   ,16b,16e,7b,174,177,7e,17d,180,81,186,189,84,18f,192,87,198,19b
  //   ,8a,1a1,1a4,8d,1aa,1ad,90,1b3,1b6,93,1bc,1bf,96,1c5,1c8,99,1ce
  //   ,1d1,9c,1d7,1da,9f,1e0,1e3,a2,1e9,1ec,a5,1f2,1f5,a8,1fb,1fe,ab
  //   ,204,207,ae,20d,210,b1,216,219,b4,21f,222,b7,228,22b,ba,231,234
  //   ,bd,23a,23d,c0,243,246,c3,24c,24f,c6,255,258,c9,25e,261,cc,267
  //   ,26a,cf,270,273,d2,279,27c,d5,282,285,d8,28b,28e,db,294,297,de
  //   ,29d,2a0,e1,2a6,2a9,e4,2af,2b2,e7,2b8,2bb,ea,2c1,2c4,ed,2ca,2cd
  //   ,f0,2d3,2d6,f3,2dc,2df,f6,2e5,2e8,f9,2ee,2f1,fc,2f7,2fa,ff,0,4,4
  //   ,c,4,14,c,1c,8,24,14,2c,c,34,1c,3c,10,44,24,4c,14,54,2c,5c,18
  //   ,64,34,6c,1c,74,3c,7c,20,84,44,8c,24,94,4c,9c,28,a4,54,ac,2c,b4
  //   ,5c,bc,30,c4,64,cc,34,d4,6c,dc,38,e4,74,ec,3c,f4,7c,fc,40,104
  //   ,84,10c,44,114,8c,11c,48,124,94,12c,4c,134,9c,13c,50,144,a4,14c
  //   ,54,154,ac,15c,58,164,b4,16c,5c,174,bc,17c,60,184,c4,18c,64,194
  //   ,cc,19c,68,1a4,d4,1ac,6c,1b4,dc,1bc,70,1c4,e4,1cc,74,1d4,ec,1dc
  //   ,78,1e4,f4,1ec,7c,1f4,fc,1fc,80,204,104,20c,84,214,10c,21c,88
  //   ,224,114,22c,8c,234,11c,23c,90,244,124,24c,94,254,12c,25c,98,264
  //   ,134,26c,9c,274,13c,27c,a0,284,144,28c,a4,294,14c,29c,a8,2a4,154
  //   ,2ac,ac,2b4,15c,2bc,b0,2c4,164,2cc,b4,2d4,16c,2dc,b8,2e4,174,2ec
  //   ,bc,2f4,17c,2fc,c0,304,184,30c,c4,314,18c,31c,c8,324,194,32c,cc
  //   ,334,19c,33c,d0,344,1a4,34c,d4,354,1ac,35c,d8,364,1b4,36c,dc,374
  //   ,1bc,37c,e0,384,1c4,38c,e4,394,1cc,39c,e8,3a4,1d4,3ac,ec,3b4,1dc
  //   ,3bc,f0,3c4,1e4,3cc,f4,3d4,1ec,3dc,f8,3e4,1f4,3ec,fc,3f4,1fc,3fc
  //   ,0,5,a,f,14,5,1e,23,28,2d,a,37,3c,41,46,f,50,55,5a,5f,14,69,6e
  //   ,73,78,19,82,87,8c,91,1e,9b,a0,a5,aa,23,b4,b9,be,c3,28,cd,d2,d7
  //   ,dc,2d,e6,eb,f0,f5,32,ff,104,109,10e,37,118,11d,122,127,3c,131
  //   ,136,13b,140,41,14a,14f,154,159,46,163,168,16d,172,4b,17c,181
  //   ,186,18b,50,195,19a,19f,1a4,55,1ae,1b3,1b8,1bd,5a,1c7,1cc,1d1
  //   ,1d6,5f,1e0,1e5,1ea,1ef,64,1f9,1fe,203,208,69,212,217,21c,221
  //   ,6e,22b,230,235,23a,73,244,249,24e,253,78,25d,262,267,26c,7d,276
  //   ,27b,280,285,82,28f,294,299,29e,87,2a8,2ad,2b2,2b7,8c,2c1,2c6
  //   ,2cb,2d0,91,2da,2df,2e4,2e9,96,2f3,2f8,2fd,302,9b,30c,311,316
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  //   accA
  //   accB
  //   regC
  //   regD
endmodule

/* Test case 26_P10T01:
M N progIn reset progLoad start result clk valid done output
0 0      0     0        0     0      0   0     x    x      x
0 0      0     0        0     0      0   1     x    x      x
0 0      0     1        0     0      0   0     x    x      x
0 0      0     1        0     0      0   1     0    0      x
0 0      0     0        0     0      0   0     0    0      x
0 0      0     0        0     0      0   1     0    0      x
0 0      0     0        0     0      0   0     0    0      x
0 0      0     0        0     0      0   1     0    0      x
0 0      0     0        0     0      0   0     0    0      x
0 0      0     0        0     0      0   1     0    0      x
0 0      0     0        0     0      0   0     0    0      x
0 0      0     0        0     0      0   1     0    0      x
0 0      0     0        0     0      0   0     0    0      x
0 0      0     0        0     0      0   1     0    0      x
0 0      0     0        0     0      0   0     0    0      x
0 0      0     0        0     0      0   1     0    0      x
0 0      0     0        0     0      0   0     0    0      x
0 0      0     0        0     0      0   1     0    0      x
0 0      0     0        0     0      0   0     0    0      x
0 0      0     0        0     0      0   1     0    0      x
0 0      0     0        0     0      0   0     0    0      x
0 0      0     0        0     0      0   1     0    0      x
0 0      0     0        0     0      0   0     0    0      x
0 0      0     0        0     0      0   1     0    0      x
0 0      0     0        0     0      0   0     0    0      x
0 0      0     0        0     0      0   1     0    0      x
0 0      0     0        0     0      0   0     0    0      x
0 0      0     0        0     0      0   1     0    0      x
0 0      0     0        0     0      0   0     0    0      x
0 0      0     0        0     0      0   1     0    0      x
0 0      0     0        0     0      0   0     0    0      x
0 0      0     0        0     0      0   1     0    0      x
0 0      0     0        0     0      0   0     0    0      x
0 0      0     0        0     0      0   1     0    0      x
0 0      0     0        0     0      0   0     0    0      x
0 0      0     0        0     0      0   1     0    0      x
0 0      0     0        0     0      0   0     0    0      x
0 0      0     0        0     0      0   1     0    0      x
0 0      0     0        0     0      0   0     0    0      x
0 0      0     0        0     0      0   1     0    0      x
0 0      0     0        0     0      0   0     0    0      x
0 0      0     0        0     0      0   1     0    0      x
0 0      0     0        0     0      0   0     0    0      x
0 0      0     0        0     0      0   1     0    0      x
0 0    262     0        1     0      0   0     0    0      x
0 0    262     0        1     0      0   1     0    0      x
0 0   4352     0        1     0      0   0     0    0      x
0 0   4352     0        1     0      0   1     0    0      x
0 0  13312     0        1     0      0   0     0    0      x
0 0  13312     0        1     0      0   1     0    0      x
0 0  16128     0        1     0      0   0     0    0      x
0 0  16128     0        1     0      0   1     0    0      x
0 0      0     0        0     0      0   0     0    0      x
0 0      0     0        0     0      0   1     0    0      x
0 0      0     0        0     0      0   0     0    0      x
0 0      0     0        0     0      0   1     0    0      x
0 0      0     0        0     0      0   0     0    0      x
0 0      0     0        0     0      0   1     0    0      x
0 0      0     0        0     1      0   0     0    0      x
0 0      0     0        0     1      0   1     0    0      x
0 0      0     0        0     0      0   0     x    0      x
0 0      0     0        0     0      0   1     x    0      x
0 0      0     0        0     0      0   0     x    0      x
0 0      0     0        0     0      0   1     x    0      x
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*/

/* Test case 28_P11T01:
M N progIn reset progLoad start result clk valid done output
0 0      0     0        0     0      0   0     x    x      x
0 0      0     0        0     0      0   1     x    x      x
0 0      0     1        0     0      0   0     x    x      x
0 0      0     1        0     0      0   1     0    0      x
0 0      0     0        0     0      0   0     0    0      x
0 0      0     0        0     0      0   1     0    0      x
0 0      0     0        0     0      0   0     0    0      x
0 0      0     0        0     0      0   1     0    0      x
0 0      0     0        0     0      0   0     0    0      x
0 0      0     0        0     0      0   1     0    0      x
0 0      0     0        0     0      0   0     0    0      x
0 0      0     0        0     0      0   1     0    0      x
0 0      0     0        0     0      0   0     0    0      x
0 0      0     0        0     0      0   1     0    0      x
0 0      0     0        0     0      0   0     0    0      x
0 0      0     0        0     0      0   1     0    0      x
0 0      0     0        0     0      0   0     0    0      x
0 0      0     0        0     0      0   1     0    0      x
0 0      0     0        0     0      0   0     0    0      x
0 0      0     0        0     0      0   1     0    0      x
0 0      0     0        0     0      0   0     0    0      x
0 0      0     0        0     0      0   1     0    0      x
0 0      0     0        0     0      0   0     0    0      x
0 0      0     0        0     0      0   1     0    0      x
0 0      0     0        0     0      0   0     0    0      x
0 0      0     0        0     0      0   1     0    0      x
0 0      0     0        0     0      0   0     0    0      x
0 0      0     0        0     0      0   1     0    0      x
0 0      0     0        0     0      0   0     0    0      x
0 0      0     0        0     0      0   1     0    0      x
0 0      0     0        0     0      0   0     0    0      x
0 0      0     0        0     0      0   1     0    0      x
0 0      0     0        0     0      0   0     0    0      x
0 0      0     0        0     0      0   1     0    0      x
0 0      0     0        0     0      0   0     0    0      x
0 0      0     0        0     0      0   1     0    0      x
0 0      0     0        0     0      0   0     0    0      x
0 0      0     0        0     0      0   1     0    0      x
0 0      0     0        0     0      0   0     0    0      x
0 0      0     0        0     0      0   1     0    0      x
0 0      0     0        0     0      0   0     0    0      x
0 0      0     0        0     0      0   1     0    0      x
0 0      0     0        0     0      0   0     0    0      x
0 0      0     0        0     0      0   1     0    0      x
0 0     27     0        1     0      0   0     0    0      x
0 0     27     0        1     0      0   1     0    0      x
0 0     60     0        1     0      0   0     0    0      x
0 0     60     0        1     0      0   1     0    0      x
0 0     30     0        1     0      0   0     0    0      x
0 0     30     0        1     0      0   1     0    0      x
0 0    255     0        1     0      0   0     0    0      x
0 0    255     0        1     0      0   1     0    0      x
0 0      6     0        1     0      0   0     0    0      x
0 0      6     0        1     0      0   1     0    0      x
0 0    251     0        1     0      0   0     0    0      x
0 0    251     0        1     0      0   1     0    0      x
0 0    127     0        1     0      0   0     0    0      x
0 0    127     0        1     0      0   1     0    0      x
0 0    120     0        1     0      0   0     0    0      x
0 0    120     0        1     0      0   1     0    0      x
0 0    232     0        1     0      0   0     0    0      x
0 0    232     0        1     0      0   1     0    0      x
0 0      0     0        1     0      0   0     0    0      x
0 0      0     0        1     0      0   1     0    0      x
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*/

/* Test case 01_P01T01:
M N progIn reset progLoad start result clk valid done output
0 0      0     0        0     0      0   0     x    x      x
0 0      0     0        0     0      0   1     x    x      x
0 0      0     1        0     0      0   0     x    x      x
0 0      0     1        0     0      0   1     0    0      x
0 0      0     0        0     0      0   0     0    0      x
0 0      0     0        0     0      0   1     0    0      x
0 0      0     0        0     0      0   0     0    0      x
0 0      0     0        0     0      0   1     0    0      x
0 0      0     0        0     0      0   0     0    0      x
0 0      0     0        0     0      0   1     0    0      x
0 0      0     0        0     0      0   0     0    0      x
0 0      0     0        0     0      0   1     0    0      x
0 0      0     0        0     0      0   0     0    0      x
0 0      0     0        0     0      0   1     0    0      x
0 0      0     0        0     0      0   0     0    0      x
0 0      0     0        0     0      0   1     0    0      x
0 0      0     0        0     0      0   0     0    0      x
0 0      0     0        0     0      0   1     0    0      x
0 0      0     0        0     0      0   0     0    0      x
0 0      0     0        0     0      0   1     0    0      x
0 0      0     0        0     0      0   0     0    0      x
0 0      0     0        0     0      0   1     0    0      x
0 0      0     0        0     0      0   0     0    0      x
0 0      0     0        0     0      0   1     0    0      x
0 0      0     0        0     0      0   0     0    0      x
0 0      0     0        0     0      0   1     0    0      x
0 0      0     0        0     0      0   0     0    0      x
0 0      0     0        0     0      0   1     0    0      x
0 0      0     0        0     0      0   0     0    0      x
0 0      0     0        0     0      0   1     0    0      x
0 0      0     0        0     0      0   0     0    0      x
0 0      0     0        0     0      0   1     0    0      x
0 0      0     0        0     0      0   0     0    0      x
0 0      0     0        0     0      0   1     0    0      x
0 0      0     0        0     0      0   0     0    0      x
0 0      0     0        0     0      0   1     0    0      x
0 0      0     0        0     0      0   0     0    0      x
0 0      0     0        0     0      0   1     0    0      x
0 0      0     0        0     0      0   0     0    0      x
0 0      0     0        0     0      0   1     0    0      x
0 0      0     0        0     0      0   0     0    0      x
0 0      0     0        0     0      0   1     0    0      x
0 0    271     0        1     0      0   0     0    0      x
0 0    271     0        1     0      0   1     0    0      x
0 0    565     0        1     0      0   0     0    0      x
0 0    565     0        1     0      0   1     0    0      x
0 0   8192     0        1     0      0   0     0    0      x
0 0   8192     0        1     0      0   1     0    0      x
0 0   4355     0        1     0      0   0     0    0      x
0 0   4355     0        1     0      0   1     0    0      x
0 0  16128     0        1     0      0   0     0    0      x
0 0  16128     0        1     0      0   1     0    0      x
0 0      0     0        0     1      0   0     0    0      x
0 0      0     0        0     1      0   1     0    0      x
0 0      0     0        0     0      0   0     x    0      x
0 0      0     0        0     0      0   1     x    0      x
0 0      0     0        0     0      0   0     x    0      x
0 0      0     0        0     0      0   1     x    0      x
0 0      0     0        0     0      0   0     x    0      x
0 0      0     0        0     0      0   1     x    0      x
0 0      0     0        0     0      0   0     x    0      x
0 0      0     0        0     0      0   1     x    0      x
0 0      0     0        0     0      0   0     x    0      x
0 0      0     0        0     0      0   1     x    0      x
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*/

/* Test case 06_P04T01:
M N progIn reset progLoad start result clk valid done output
0 0      0     0        0     0      0   0     x    x      x
0 0      0     0        0     0      0   1     x    x      x
0 0      0     1        0     0      0   0     x    x      x
0 0      0     1        0     0      0   1     0    0      x
0 0      0     0        0     0      0   0     0    0      x
0 0      0     0        0     0      0   1     0    0      x
0 0      0     0        0     0      0   0     0    0      x
0 0      0     0        0     0      0   1     0    0      x
0 0      0     0        0     0      0   0     0    0      x
0 0      0     0        0     0      0   1     0    0      x
0 0      0     0        0     0      0   0     0    0      x
0 0      0     0        0     0      0   1     0    0      x
0 0      0     0        0     0      0   0     0    0      x
0 0      0     0        0     0      0   1     0    0      x
0 0      0     0        0     0      0   0     0    0      x
0 0      0     0        0     0      0   1     0    0      x
0 0      0     0        0     0      0   0     0    0      x
0 0      0     0        0     0      0   1     0    0      x
0 0      0     0        0     0      0   0     0    0      x
0 0      0     0        0     0      0   1     0    0      x
0 0      0     0        0     0      0   0     0    0      x
0 0      0     0        0     0      0   1     0    0      x
0 0      0     0        0     0      0   0     0    0      x
0 0      0     0        0     0      0   1     0    0      x
0 0      0     0        0     0      0   0     0    0      x
0 0      0     0        0     0      0   1     0    0      x
0 0      0     0        0     0      0   0     0    0      x
0 0      0     0        0     0      0   1     0    0      x
0 0      0     0        0     0      0   0     0    0      x
0 0      0     0        0     0      0   1     0    0      x
0 0      0     0        0     0      0   0     0    0      x
0 0      0     0        0     0      0   1     0    0      x
0 0      0     0        0     0      0   0     0    0      x
0 0      0     0        0     0      0   1     0    0      x
0 0      0     0        0     0      0   0     0    0      x
0 0      0     0        0     0      0   1     0    0      x
0 0      0     0        0     0      0   0     0    0      x
0 0      0     0        0     0      0   1     0    0      x
0 0      0     0        0     0      0   0     0    0      x
0 0      0     0        0     0      0   1     0    0      x
0 0      0     0        0     0      0   0     0    0      x
0 0      0     0        0     0      0   1     0    0      x
0 0      0     0        0     0      0   0     0    0      x
0 0      0     0        0     0      0   1     0    0      x
0 0    271     0        1     0      0   0     0    0      x
0 0    271     0        1     0      0   1     0    0      x
0 0  12544     0        1     0      0   0     0    0      x
0 0  12544     0        1     0      0   1     0    0      x
0 0   4864     0        1     0      0   0     0    0      x
0 0   4864     0        1     0      0   1     0    0      x
0 0    257     0        1     0      0   0     0    0      x
0 0    257     0        1     0      0   1     0    0      x
0 0   4867     0        1     0      0   0     0    0      x
0 0   4867     0        1     0      0   1     0    0      x
0 0    455     0        1     0      0   0     0    0      x
0 0    455     0        1     0      0   1     0    0      x
0 0  12544     0        1     0      0   0     0    0      x
0 0  12544     0        1     0      0   1     0    0      x
0 0   4873     0        1     0      0   0     0    0      x
0 0   4873     0        1     0      0   1     0    0      x
0 0   4354     0        1     0      0   0     0    0      x
0 0   4354     0        1     0      0   1     0    0      x
0 0   4355     0        1     0      0   0     0    0      x
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*/

/* Test case 11_P07T02:
M N progIn reset progLoad start result clk valid done output
0 0      0     0        0     0      0   0     x    x      x
0 0      0     0        0     0      0   1     x    x      x
0 0      0     1        0     0      0   0     x    x      x
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*/

/* Test case 02_P01T02:
M N progIn reset progLoad start result clk valid done output
0 0      0     0        0     0      0   0     x    x      x
0 0      0     0        0     0      0   1     x    x      x
0 0      0     1        0     0      0   0     x    x      x
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*/

/* Test case 07_P05T01:
M N progIn reset progLoad start result clk valid done output
0 0      0     0        0     0      0   0     x    x      x
0 0      0     0        0     0      0   1     x    x      x
0 0      0     1        0     0      0   0     x    x      x
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*/

/* Test case 12_P08T01:
M N progIn reset progLoad start result clk valid done output
0 0      0     0        0     0      0   0     x    x      x
0 0      0     0        0     0      0   1     x    x      x
0 0      0     1        0     0      0   0     x    x      x
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*/

/* Test case 03_P02T01:
M N progIn reset progLoad start result clk valid done output
0 0      0     0        0     0      0   0     x    x      x
0 0      0     0        0     0      0   1     x    x      x
0 0      0     1        0     0      0   0     x    x      x
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*/

/* Test case 08_P06T01:
M N progIn reset progLoad start result clk valid done output
0 0      0     0        0     0      0   0     x    x      x
0 0      0     0        0     0      0   1     x    x      x
0 0      0     1        0     0      0   0     x    x      x
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*/

/* Test case 13_P08T02:
M N progIn reset progLoad start result clk valid done output
0 0      0     0        0     0      0   0     x    x      x
0 0      0     0        0     0      0   1     x    x      x
0 0      0     1        0     0      0   0     x    x      x
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*/

/* Test case 04_P03T01:
M N progIn reset progLoad start result clk valid done output
0 0      0     0        0     0      0   0     x    x      x
0 0      0     0        0     0      0   1     x    x      x
0 0      0     1        0     0      0   0     x    x      x
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*/

/* Test case 09_P06T02:
M N progIn reset progLoad start result clk valid done output
0 0      0     0        0     0      0   0     x    x      x
0 0      0     0        0     0      0   1     x    x      x
0 0      0     1        0     0      0   0     x    x      x
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*/

/* Test case 14_P09T01:
M N progIn reset progLoad start result clk valid done output
0 0      0     0        0     0      0   0     x    x      x
0 0      0     0        0     0      0   1     x    x      x
0 0      0     1        0     0      0   0     x    x      x
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*/

/* Test case 05_P03T02:
M N progIn reset progLoad start result clk valid done output
0 0      0     0        0     0      0   0     x    x      x
0 0      0     0        0     0      0   1     x    x      x
0 0      0     1        0     0      0   0     x    x      x
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*/

/* Test case 10_P07T01:
M N progIn reset progLoad start result clk valid done output
0 0      0     0        0     0      0   0     x    x      x
0 0      0     0        0     0      0   1     x    x      x
0 0      0     1        0     0      0   0     x    x      x
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*/

/* Test case 15_P09T02:
M N progIn reset progLoad start result clk valid done output
0 0      0     0        0     0      0   0     x    x      x
0 0      0     0        0     0      0   1     x    x      x
0 0      0     1        0     0      0   0     x    x      x
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*/
