// Digital circuit TEMPLATE Project Full Testcase 2568.dig as structural Verilog
module TEMPLATE_Project_Full_Testcase_2568 (
  input  [7:0] M,
  input  [7:0] N,
  input  [13:0] progIn,
  input  reset,
  input  progLoad,
  input  start,
  input  result,
  input  clk,
  output valid,
  output done,
  output [7:0] \output 
);

  RAMDualAccess #(.AddrBits(8), .Bits(14)) pRAM ();  // open: str, C, ld, A1, Din1, A2, D1, D2
  RAMDualAccess #(.AddrBits(8), .Bits(8)) rRAM ();  // open: str, C, ld, A1, Din1, A2, D1, D2
  Seven_Seg_Hex seven_seg_hex_1 (.d(\output [7:4]), .dp(1'b0));
  Seven_Seg_Hex seven_seg_hex_2 (.d(\output [3:0]), .dp(1'b0));
endmodule

/* Test case 01_P01T2:
M N progIn reset progLoad start result clk valid done output
0 0      0     0        0     0      0   0     x    x      x
0 0      0     0        0     0      0   1     x    x      x
0 0      0     1        0     0      0   0     x    x      x
0 0      0     1        0     0      0   1     0    0      x
0 0      0     0        0     0      0   0     0    0      x
0 0      0     0        0     0      0   1     0    0      x
0 0      0     0        0     0      0   0     0    0      x
0 0      0     0        0     0      0   1     0    0      x
0 0      0     0        0     0      0   0     0    0      x
0 0      0     0        0     0      0   1     0    0      x
0 0      0     0        0     0      0   0     0    0      x
0 0      0     0        0     0      0   1     0    0      x
0 0      0     0        0     0      0   0     0    0      x
0 0      0     0        0     0      0   1     0    0      x
0 0      0     0        0     0      0   0     0    0      x
0 0      0     0        0     0      0   1     0    0      x
0 0      0     0        0     0      0   0     0    0      x
0 0      0     0        0     0      0   1     0    0      x
0 0      0     0        0     0      0   0     0    0      x
0 0      0     0        0     0      0   1     0    0      x
0 0      0     0        0     0      0   0     0    0      x
0 0      0     0        0     0      0   1     0    0      x
0 0      0     0        0     0      0   0     0    0      x
0 0      0     0        0     0      0   1     0    0      x
0 0      0     0        0     0      0   0     0    0      x
0 0      0     0        0     0      0   1     0    0      x
0 0      0     0        0     0      0   0     0    0      x
0 0      0     0        0     0      0   1     0    0      x
0 0      0     0        0     0      0   0     0    0      x
0 0      0     0        0     0      0   1     0    0      x
0 0      0     0        0     0      0   0     0    0      x
0 0      0     0        0     0      0   1     0    0      x
0 0      0     0        0     0      0   0     0    0      x
0 0      0     0        0     0      0   1     0    0      x
0 0      0     0        0     0      0   0     0    0      x
0 0      0     0        0     0      0   1     0    0      x
0 0      0     0        0     0      0   0     0    0      x
0 0      0     0        0     0      0   1     0    0      x
0 0      0     0        0     0      0   0     0    0      x
0 0      0     0        0     0      0   1     0    0      x
0 0      0     0        0     0      0   0     0    0      x
0 0      0     0        0     0      0   1     0    0      x
0 0    271     0        1     0      0   0     0    0      x
0 0    271     0        1     0      0   1     0    0      x
0 0    565     0        1     0      0   0     0    0      x
0 0    565     0        1     0      0   1     0    0      x
0 0   8192     0        1     0      0   0     0    0      x
0 0   8192     0        1     0      0   1     0    0      x
0 0   4355     0        1     0      0   0     0    0      x
0 0   4355     0        1     0      0   1     0    0      x
0 0  16128     0        1     0      0   0     0    0      x
0 0  16128     0        1     0      0   1     0    0      x
0 0      0     0        0     1      0   0     0    0      x
0 0      0     0        0     1      0   1     0    0      x
0 0      0     0        0     0      0   0     x    0      x
0 0      0     0        0     0      0   1     x    0      x
0 0      0     0        0     0      0   0     x    0      x
0 0      0     0        0     0      0   1     x    0      x
0 0      0     0        0     0      0   0     x    0      x
0 0      0     0        0     0      0   1     x    0      x
0 0      0     0        0     0      0   0     x    0      x
0 0      0     0        0     0      0   1     x    0      x
0 0      0     0        0     0      0   0     x    0      x
0 0      0     0        0     0      0   1     x    0      x
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*/

/* Test case 06_P04T2:
M N progIn reset progLoad start result clk valid done output
0 0      0     0        0     0      0   0     x    x      x
0 0      0     0        0     0      0   1     x    x      x
0 0      0     1        0     0      0   0     x    x      x
0 0      0     1        0     0      0   1     0    0      x
0 0      0     0        0     0      0   0     0    0      x
0 0      0     0        0     0      0   1     0    0      x
0 0      0     0        0     0      0   0     0    0      x
0 0      0     0        0     0      0   1     0    0      x
0 0      0     0        0     0      0   0     0    0      x
0 0      0     0        0     0      0   1     0    0      x
0 0      0     0        0     0      0   0     0    0      x
0 0      0     0        0     0      0   1     0    0      x
0 0      0     0        0     0      0   0     0    0      x
0 0      0     0        0     0      0   1     0    0      x
0 0      0     0        0     0      0   0     0    0      x
0 0      0     0        0     0      0   1     0    0      x
0 0      0     0        0     0      0   0     0    0      x
0 0      0     0        0     0      0   1     0    0      x
0 0      0     0        0     0      0   0     0    0      x
0 0      0     0        0     0      0   1     0    0      x
0 0      0     0        0     0      0   0     0    0      x
0 0      0     0        0     0      0   1     0    0      x
0 0      0     0        0     0      0   0     0    0      x
0 0      0     0        0     0      0   1     0    0      x
0 0      0     0        0     0      0   0     0    0      x
0 0      0     0        0     0      0   1     0    0      x
0 0      0     0        0     0      0   0     0    0      x
0 0      0     0        0     0      0   1     0    0      x
0 0      0     0        0     0      0   0     0    0      x
0 0      0     0        0     0      0   1     0    0      x
0 0      0     0        0     0      0   0     0    0      x
0 0      0     0        0     0      0   1     0    0      x
0 0      0     0        0     0      0   0     0    0      x
0 0      0     0        0     0      0   1     0    0      x
0 0      0     0        0     0      0   0     0    0      x
0 0      0     0        0     0      0   1     0    0      x
0 0      0     0        0     0      0   0     0    0      x
0 0      0     0        0     0      0   1     0    0      x
0 0      0     0        0     0      0   0     0    0      x
0 0      0     0        0     0      0   1     0    0      x
0 0      0     0        0     0      0   0     0    0      x
0 0      0     0        0     0      0   1     0    0      x
0 0      0     0        0     0      0   0     0    0      x
0 0      0     0        0     0      0   1     0    0      x
0 0    271     0        1     0      0   0     0    0      x
0 0    271     0        1     0      0   1     0    0      x
0 0  12544     0        1     0      0   0     0    0      x
0 0  12544     0        1     0      0   1     0    0      x
0 0   4864     0        1     0      0   0     0    0      x
0 0   4864     0        1     0      0   1     0    0      x
0 0    257     0        1     0      0   0     0    0      x
0 0    257     0        1     0      0   1     0    0      x
0 0   4867     0        1     0      0   0     0    0      x
0 0   4867     0        1     0      0   1     0    0      x
0 0    455     0        1     0      0   0     0    0      x
0 0    455     0        1     0      0   1     0    0      x
0 0  12544     0        1     0      0   0     0    0      x
0 0  12544     0        1     0      0   1     0    0      x
0 0   4873     0        1     0      0   0     0    0      x
0 0   4873     0        1     0      0   1     0    0      x
0 0   4354     0        1     0      0   0     0    0      x
0 0   4354     0        1     0      0   1     0    0      x
0 0   4355     0        1     0      0   0     0    0      x
0 0   4355     0        1     0      0   1     0    0      x
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*/

/* Test case 11_P07T3:
M N progIn reset progLoad start result clk valid done output
0 0      0     0        0     0      0   0     x    x      x
0 0      0     0        0     0      0   1     x    x      x
0 0      0     1        0     0      0   0     x    x      x
0 0      0     1        0     0      0   1     0    0      x
0 0      0     0        0     0      0   0     0    0      x
0 0      0     0        0     0      0   1     0    0      x
0 0      0     0        0     0      0   0     0    0      x
0 0      0     0        0     0      0   1     0    0      x
0 0      0     0        0     0      0   0     0    0      x
0 0      0     0        0     0      0   1     0    0      x
0 0      0     0        0     0      0   0     0    0      x
0 0      0     0        0     0      0   1     0    0      x
0 0      0     0        0     0      0   0     0    0      x
0 0      0     0        0     0      0   1     0    0      x
0 0      0     0        0     0      0   0     0    0      x
0 0      0     0        0     0      0   1     0    0      x
0 0      0     0        0     0      0   0     0    0      x
0 0      0     0        0     0      0   1     0    0      x
0 0      0     0        0     0      0   0     0    0      x
0 0      0     0        0     0      0   1     0    0      x
0 0      0     0        0     0      0   0     0    0      x
0 0      0     0        0     0      0   1     0    0      x
0 0      0     0        0     0      0   0     0    0      x
0 0      0     0        0     0      0   1     0    0      x
0 0      0     0        0     0      0   0     0    0      x
0 0      0     0        0     0      0   1     0    0      x
0 0      0     0        0     0      0   0     0    0      x
0 0      0     0        0     0      0   1     0    0      x
0 0      0     0        0     0      0   0     0    0      x
0 0      0     0        0     0      0   1     0    0      x
0 0      0     0        0     0      0   0     0    0      x
0 0      0     0        0     0      0   1     0    0      x
0 0      0     0        0     0      0   0     0    0      x
0 0      0     0        0     0      0   1     0    0      x
0 0      0     0        0     0      0   0     0    0      x
0 0      0     0        0     0      0   1     0    0      x
0 0      0     0        0     0      0   0     0    0      x
0 0      0     0        0     0      0   1     0    0      x
0 0      0     0        0     0      0   0     0    0      x
0 0      0     0        0     0      0   1     0    0      x
0 0      0     0        0     0      0   0     0    0      x
0 0      0     0        0     0      0   1     0    0      x
0 0      0     0        0     0      0   0     0    0      x
0 0      0     0        0     0      0   1     0    0      x
0 0    446     0        1     0      0   0     0    0      x
0 0    446     0        1     0      0   1     0    0      x
0 0   4353     0        1     0      0   0     0    0      x
0 0   4353     0        1     0      0   1     0    0      x
0 0    426     0        1     0      0   0     0    0      x
0 0    426     0        1     0      0   1     0    0      x
0 0   4367     0        1     0      0   0     0    0      x
0 0   4367     0        1     0      0   1     0    0      x
0 0  13087     0        1     0      0   0     0    0      x
0 0  13087     0        1     0      0   1     0    0      x
0 0  16128     0        1     0      0   0     0    0      x
0 0  16128     0        1     0      0   1     0    0      x
0 0      0     0        0     0      0   0     0    0      x
0 0      0     0        0     0      0   1     0    0      x
0 0      0     0        0     1      0   0     0    0      x
0 0      0     0        0     1      0   1     0    0      x
0 0      0     0        0     0      0   0     x    0      x
0 0      0     0        0     0      0   1     x    0      x
0 0      0     0        0     0      0   0     x    0      x
0 0      0     0        0     0      0   1     x    0      x
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*/

/* Test case 02_P01T3:
M N progIn reset progLoad start result clk valid done output
0 0      0     0        0     0      0   0     x    x      x
0 0      0     0        0     0      0   1     x    x      x
0 0      0     1        0     0      0   0     x    x      x
0 0      0     1        0     0      0   1     0    0      x
0 0      0     0        0     0      0   0     0    0      x
0 0      0     0        0     0      0   1     0    0      x
0 0      0     0        0     0      0   0     0    0      x
0 0      0     0        0     0      0   1     0    0      x
0 0      0     0        0     0      0   0     0    0      x
0 0      0     0        0     0      0   1     0    0      x
0 0      0     0        0     0      0   0     0    0      x
0 0      0     0        0     0      0   1     0    0      x
0 0      0     0        0     0      0   0     0    0      x
0 0      0     0        0     0      0   1     0    0      x
0 0      0     0        0     0      0   0     0    0      x
0 0      0     0        0     0      0   1     0    0      x
0 0      0     0        0     0      0   0     0    0      x
0 0      0     0        0     0      0   1     0    0      x
0 0      0     0        0     0      0   0     0    0      x
0 0      0     0        0     0      0   1     0    0      x
0 0      0     0        0     0      0   0     0    0      x
0 0      0     0        0     0      0   1     0    0      x
0 0      0     0        0     0      0   0     0    0      x
0 0      0     0        0     0      0   1     0    0      x
0 0      0     0        0     0      0   0     0    0      x
0 0      0     0        0     0      0   1     0    0      x
0 0      0     0        0     0      0   0     0    0      x
0 0      0     0        0     0      0   1     0    0      x
0 0      0     0        0     0      0   0     0    0      x
0 0      0     0        0     0      0   1     0    0      x
0 0      0     0        0     0      0   0     0    0      x
0 0      0     0        0     0      0   1     0    0      x
0 0      0     0        0     0      0   0     0    0      x
0 0      0     0        0     0      0   1     0    0      x
0 0      0     0        0     0      0   0     0    0      x
0 0      0     0        0     0      0   1     0    0      x
0 0      0     0        0     0      0   0     0    0      x
0 0      0     0        0     0      0   1     0    0      x
0 0      0     0        0     0      0   0     0    0      x
0 0      0     0        0     0      0   1     0    0      x
0 0      0     0        0     0      0   0     0    0      x
0 0      0     0        0     0      0   1     0    0      x
0 0    271     0        1     0      0   0     0    0      x
0 0    271     0        1     0      0   1     0    0      x
0 0    565     0        1     0      0   0     0    0      x
0 0    565     0        1     0      0   1     0    0      x
0 0   8192     0        1     0      0   0     0    0      x
0 0   8192     0        1     0      0   1     0    0      x
0 0   4355     0        1     0      0   0     0    0      x
0 0   4355     0        1     0      0   1     0    0      x
0 0  16128     0        1     0      0   0     0    0      x
0 0  16128     0        1     0      0   1     0    0      x
0 0      0     0        0     1      0   0     0    0      x
0 0      0     0        0     1      0   1     0    0      x
0 0      0     0        0     0      0   0     x    0      x
0 0      0     0        0     0      0   1     x    0      x
0 0      0     0        0     0      0   0     x    0      x
0 0      0     0        0     0      0   1     x    0      x
0 0      0     0        0     0      0   0     x    0      x
0 0      0     0        0     0      0   1     x    0      x
0 0      0     0        0     0      0   0     x    0      x
0 0      0     0        0     0      0   1     x    0      x
0 0      0     0        0     0      0   0     x    0      x
0 0      0     0        0     0      0   1     x    0      x
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*/

/* Test case 07_P05T2:
M N progIn reset progLoad start result clk valid done output
0 0      0     0        0     0      0   0     x    x      x
0 0      0     0        0     0      0   1     x    x      x
0 0      0     1        0     0      0   0     x    x      x
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*/

/* Test case 12_P08T2:
M N progIn reset progLoad start result clk valid done output
0 0      0     0        0     0      0   0     x    x      x
0 0      0     0        0     0      0   1     x    x      x
0 0      0     1        0     0      0   0     x    x      x
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*/

/* Test case 03_P02T2:
M N progIn reset progLoad start result clk valid done output
0 0      0     0        0     0      0   0     x    x      x
0 0      0     0        0     0      0   1     x    x      x
0 0      0     1        0     0      0   0     x    x      x
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*/

/* Test case 08_P06T2:
M N progIn reset progLoad start result clk valid done output
0 0      0     0        0     0      0   0     x    x      x
0 0      0     0        0     0      0   1     x    x      x
0 0      0     1        0     0      0   0     x    x      x
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*/

/* Test case 13_P08T3:
M N progIn reset progLoad start result clk valid done output
0 0      0     0        0     0      0   0     x    x      x
0 0      0     0        0     0      0   1     x    x      x
0 0      0     1        0     0      0   0     x    x      x
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*/

/* Test case 04_P03T2:
M N progIn reset progLoad start result clk valid done output
0 0      0     0        0     0      0   0     x    x      x
0 0      0     0        0     0      0   1     x    x      x
0 0      0     1        0     0      0   0     x    x      x
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*/

/* Test case 09_P06T3:
M N progIn reset progLoad start result clk valid done output
0 0      0     0        0     0      0   0     x    x      x
0 0      0     0        0     0      0   1     x    x      x
0 0      0     1        0     0      0   0     x    x      x
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*/

/* Test case 14_P09T2:
M N progIn reset progLoad start result clk valid done output
0 0      0     0        0     0      0   0     x    x      x
0 0      0     0        0     0      0   1     x    x      x
0 0      0     1        0     0      0   0     x    x      x
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*/

/* Test case 05_P03T3:
M N progIn reset progLoad start result clk valid done output
0 0      0     0        0     0      0   0     x    x      x
0 0      0     0        0     0      0   1     x    x      x
0 0      0     1        0     0      0   0     x    x      x
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*/

/* Test case 10_P07T2:
M N progIn reset progLoad start result clk valid done output
0 0      0     0        0     0      0   0     x    x      x
0 0      0     0        0     0      0   1     x    x      x
0 0      0     1        0     0      0   0     x    x      x
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*/

/* Test case 15_P09T3:
M N progIn reset progLoad start result clk valid done output
0 0      0     0        0     0      0   0     x    x      x
0 0      0     0        0     0      0   1     x    x      x
0 0      0     1        0     0      0   0     x    x      x
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*/

/* Test case 01_P01T01:
M N progIn reset progLoad start result clk valid done output
0 0      0     0        0     0      0   0     x    x      x
0 0      0     0        0     0      0   1     x    x      x
0 0      0     1        0     0      0   0     x    x      x
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*/

/* Test case 06_P04T01:
M N progIn reset progLoad start result clk valid done output
0 0      0     0        0     0      0   0     x    x      x
0 0      0     0        0     0      0   1     x    x      x
0 0      0     1        0     0      0   0     x    x      x
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*/

/* Test case 11_P07T02:
M N progIn reset progLoad start result clk valid done output
0 0      0     0        0     0      0   0     x    x      x
0 0      0     0        0     0      0   1     x    x      x
0 0      0     1        0     0      0   0     x    x      x
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*/

/* Test case 16_P01T03:
M N progIn reset progLoad start result clk valid done output
0 0      0     0        0     0      0   0     x    x      x
0 0      0     0        0     0      0   1     x    x      x
0 0      0     1        0     0      0   0     x    x      x
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*/

/* Test case 21_P05T2:
M N progIn reset progLoad start result clk valid done output
0 0      0     0        0     0      0   0     x    x      x
0 0      0     0        0     0      0   1     x    x      x
0 0      0     1        0     0      0   0     x    x      x
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*/

/* Test case 26_P10T01:
M N progIn reset progLoad start result clk valid done output
0 0      0     0        0     0      0   0     x    x      x
0 0      0     0        0     0      0   1     x    x      x
0 0      0     1        0     0      0   0     x    x      x
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*/

/* Test case 02_P01T02:
M N progIn reset progLoad start result clk valid done output
0 0      0     0        0     0      0   0     x    x      x
0 0      0     0        0     0      0   1     x    x      x
0 0      0     1        0     0      0   0     x    x      x
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*/

/* Test case 07_P05T01:
M N progIn reset progLoad start result clk valid done output
0 0      0     0        0     0      0   0     x    x      x
0 0      0     0        0     0      0   1     x    x      x
0 0      0     1        0     0      0   0     x    x      x
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*/

/* Test case 12_P08T01:
M N progIn reset progLoad start result clk valid done output
0 0      0     0        0     0      0   0     x    x      x
0 0      0     0        0     0      0   1     x    x      x
0 0      0     1        0     0      0   0     x    x      x
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*/

/* Test case 17_P02T02:
M N progIn reset progLoad start result clk valid done output
0 0      0     0        0     0      0   0     x    x      x
0 0      0     0        0     0      0   1     x    x      x
0 0      0     1        0     0      0   0     x    x      x
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*/

/* Test case 22_P06T03:
M N progIn reset progLoad start result clk valid done output
0 0      0     0        0     0      0   0     x    x      x
0 0      0     0        0     0      0   1     x    x      x
0 0      0     1        0     0      0   0     x    x      x
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*/

/* Test case 27_P10T02:
M N progIn reset progLoad start result clk valid done output
0 0      0     0        0     0      0   0     x    x      x
0 0      0     0        0     0      0   1     x    x      x
0 0      0     1        0     0      0   0     x    x      x
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*/

/* Test case 03_P02T01:
M N progIn reset progLoad start result clk valid done output
0 0      0     0        0     0      0   0     x    x      x
0 0      0     0        0     0      0   1     x    x      x
0 0      0     1        0     0      0   0     x    x      x
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*/

/* Test case 08_P06T01:
M N progIn reset progLoad start result clk valid done output
0 0      0     0        0     0      0   0     x    x      x
0 0      0     0        0     0      0   1     x    x      x
0 0      0     1        0     0      0   0     x    x      x
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*/

/* Test case 13_P08T02:
M N progIn reset progLoad start result clk valid done output
0 0      0     0        0     0      0   0     x    x      x
0 0      0     0        0     0      0   1     x    x      x
0 0      0     1        0     0      0   0     x    x      x
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*/

/* Test case 18_P03T03:
M N progIn reset progLoad start result clk valid done output
0 0      0     0        0     0      0   0     x    x      x
0 0      0     0        0     0      0   1     x    x      x
0 0      0     1        0     0      0   0     x    x      x
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*/

/* Test case 23_P07T03:
M N progIn reset progLoad start result clk valid done output
0 0      0     0        0     0      0   0     x    x      x
0 0      0     0        0     0      0   1     x    x      x
0 0      0     1        0     0      0   0     x    x      x
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*/

/* Test case 28_P11T01:
M N progIn reset progLoad start result clk valid done output
0 0      0     0        0     0      0   0     x    x      x
0 0      0     0        0     0      0   1     x    x      x
0 0      0     1        0     0      0   0     x    x      x
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*/

/* Test case 04_P03T01:
M N progIn reset progLoad start result clk valid done output
0 0      0     0        0     0      0   0     x    x      x
0 0      0     0        0     0      0   1     x    x      x
0 0      0     1        0     0      0   0     x    x      x
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*/

/* Test case 09_P06T02:
M N progIn reset progLoad start result clk valid done output
0 0      0     0        0     0      0   0     x    x      x
0 0      0     0        0     0      0   1     x    x      x
0 0      0     1        0     0      0   0     x    x      x
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*/

/* Test case 14_P09T01:
M N progIn reset progLoad start result clk valid done output
0 0      0     0        0     0      0   0     x    x      x
0 0      0     0        0     0      0   1     x    x      x
0 0      0     1        0     0      0   0     x    x      x
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*/

/* Test case 19_P04T02:
M N progIn reset progLoad start result clk valid done output
0 0      0     0        0     0      0   0     x    x      x
0 0      0     0        0     0      0   1     x    x      x
0 0      0     1        0     0      0   0     x    x      x
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*/

/* Test case 24_P08T03:
M N progIn reset progLoad start result clk valid done output
0 0      0     0        0     0      0   0     x    x      x
0 0      0     0        0     0      0   1     x    x      x
0 0      0     1        0     0      0   0     x    x      x
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*/

/* Test case 29_P11T02:
M N progIn reset progLoad start result clk valid done output
0 0      0     0        0     0      0   0     x    x      x
0 0      0     0        0     0      0   1     x    x      x
0 0      0     1        0     0      0   0     x    x      x
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*/

/* Test case 05_P03T02:
M N progIn reset progLoad start result clk valid done output
0 0      0     0        0     0      0   0     x    x      x
0 0      0     0        0     0      0   1     x    x      x
0 0      0     1        0     0      0   0     x    x      x
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*/

/* Test case 10_P07T01:
M N progIn reset progLoad start result clk valid done output
0 0      0     0        0     0      0   0     x    x      x
0 0      0     0        0     0      0   1     x    x      x
0 0      0     1        0     0      0   0     x    x      x
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*/

/* Test case 15_P09T02:
M N progIn reset progLoad start result clk valid done output
0 0      0     0        0     0      0   0     x    x      x
0 0      0     0        0     0      0   1     x    x      x
0 0      0     1        0     0      0   0     x    x      x
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*/

/* Test case 20_P04T03:
M N progIn reset progLoad start result clk valid done output
0 0      0     0        0     0      0   0     x    x      x
0 0      0     0        0     0      0   1     x    x      x
0 0      0     1        0     0      0   0     x    x      x
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*/

/* Test case 25_P09T03:
M N progIn reset progLoad start result clk valid done output
0 0      0     0        0     0      0   0     x    x      x
0 0      0     0        0     0      0   1     x    x      x
0 0      0     1        0     0      0   0     x    x      x
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*/
