// Digital circuit 2_04.dig as structural Verilog
module _2_04 (
  input  A,
  input  B,
  input  Cin,
  output Sum,
  output Cout
);

  wire and_1_out, and_3_out, na, nb, nc, not_4_out, or_1_out, or_2_out, or_3_out, or_4_out, or_5_out,
       or_6_out, or_7_out;

  not not_1 (na, A);
  not not_2 (nb, B);
  not not_3 (nc, Cin);
  or or_1 (or_1_out, A, B);
  or or_2 (or_2_out, na, nb);
  and and_1 (and_1_out, or_1_out, or_2_out);
  not not_4 (not_4_out, and_1_out);
  or or_3 (or_3_out, and_1_out, Cin);
  or or_4 (or_4_out, not_4_out, nc);
  and and_2 (Sum, or_3_out, or_4_out);
  or or_5 (or_5_out, na, nc);
  or or_6 (or_6_out, na, nb);
  or or_7 (or_7_out, nc, nb);
  and and_3 (and_3_out, or_6_out, or_7_out, or_5_out);
  not not_5 (Cout, and_3_out);

  // Other names for the same wires on the sheet: c = Cin
endmodule
