// Digital circuit 2_06.dig as structural Verilog
module _2_06 (
  input  A,
  input  B,
  input  C,
  input  D,
  output Z2,
  output Z1,
  output Z3
);

  wire and_1_out, and_2_out, and_3_out, and_4_out, not_1_out, not_2_out, not_3_out, not_4_out, not_7_out,
       not_8_out, or_1_out, or_2_out, or_3_out, or_4_out, or_5_out, or_6_out, or_7_out, or_8_out, or_9_out,
       or_10_out;

  not not_1 (not_1_out, A);
  not not_2 (not_2_out, B);
  not not_3 (not_3_out, C);
  not not_4 (not_4_out, D);
  or or_1 (or_1_out, not_1_out, C);
  or or_2 (or_2_out, not_2_out, C, D);
  or or_3 (or_3_out, not_1_out, not_2_out, D);
  or or_4 (or_4_out, A, not_3_out);
  or or_5 (or_5_out, A, B, not_4_out);
  or or_6 (or_6_out, B, not_3_out, not_4_out);
  or or_7 (or_7_out, A, C);
  or or_8 (or_8_out, not_1_out, not_3_out);
  or or_9 (or_9_out, B, D);
  or or_10 (or_10_out, not_2_out, not_4_out);
  and and_1 (and_1_out, or_1_out, or_2_out, or_3_out);
  and and_2 (and_2_out, or_4_out, or_5_out, or_6_out);
  and and_3 (and_3_out, or_7_out, or_8_out);
  and and_4 (and_4_out, or_9_out, or_10_out);
  not not_5 (Z1, and_1_out);
  not not_6 (Z2, and_2_out);
  not not_7 (not_7_out, and_3_out);
  and and_5 (Z3, not_7_out, not_8_out);
  not not_8 (not_8_out, and_4_out);
endmodule
