// Digital circuit 2_07.dig as structural Verilog
module _2_07 (
  input  X0,
  input  X1,
  input  Selector,
  output Z
);

  wire and_1_out, and_2_out, not_3_out;

  // Not not_1 has open pins: in=X0, out=open
  // Not not_2 has open pins: in=X1, out=open
  not not_3 (not_3_out, Selector);
  and and_1 (and_1_out, not_3_out, X0);
  and and_2 (and_2_out, Selector, X1);
  or or_1 (Z, and_1_out, and_2_out);
endmodule
