// Digital circuit 2_09.dig as structural Verilog
module _2_09 (
  input  X0,
  input  X1,
  input  S1,
  input  X2,
  input  X3,
  input  S0,
  output Z
);

  wire and_1_out, and_2_out, and_3_out, and_4_out, not_4_out, not_6_out;

  // Not not_1 has open pins: in=X0, out=open
  // Not not_2 has open pins: in=X1, out=open
  // Not not_3 has open pins: in=X2, out=open
  not not_4 (not_4_out, S1);
  // Not not_5 has open pins: in=X3, out=open
  not not_6 (not_6_out, S0);
  and and_1 (and_1_out, X0, not_4_out, not_6_out);
  and and_2 (and_2_out, X1, not_4_out, S0);
  and and_3 (and_3_out, X2, S1, not_6_out);
  and and_4 (and_4_out, X3, S1, S0);
  or or_1 (Z, and_1_out, and_2_out, and_3_out, and_4_out);
endmodule
