// Digital circuit 3_01.dig as structural Verilog
module _3_01 (
  input  [3:0] In,
  output A,
  output B,
  output C,
  output D,
  output E,
  output F,
  output G
);

  wire and_1_out, and_2_out, and_3_out, and_4_out, and_5_out, and_6_out, and_7_out, and_8_out, and_9_out,
       and_10_out, and_11_out, and_12_out, and_13_out, and_14_out, and_15_out, and_16_out, and_17_out,
       and_18_out, not_1_out, not_2_out, not_3_out, not_4_out, or_4_out, or_5_out, or_6_out, or_7_out;

  not not_1 (not_1_out, In[3]);
  not not_2 (not_2_out, In[2]);
  not not_3 (not_3_out, In[1]);
  not not_4 (not_4_out, In[0]);
  and and_1 (and_1_out, In[2], In[0]);
  and and_2 (and_2_out, not_2_out, not_4_out);
  and and_3 (and_3_out, In[1], In[0]);
  and and_4 (and_4_out, not_3_out, not_4_out);
  and and_5 (and_5_out, not_1_out, not_2_out, not_3_out, In[0]);
  and and_6 (and_6_out, In[2], In[1], In[0]);
  and and_7 (and_7_out, In[2], not_3_out, not_4_out);
  and and_8 (and_8_out, In[3], In[1]);
  and and_9 (and_9_out, In[3], In[2]);
  and and_10 (and_10_out, In[2], not_3_out, not_4_out);
  and and_11 (and_11_out, In[3], In[0]);
  and and_12 (and_12_out, not_1_out, not_2_out, not_3_out, In[0]);
  and and_13 (and_13_out, not_2_out, In[1]);
  and and_14 (and_14_out, In[3], In[2]);
  and and_15 (and_15_out, not_1_out, not_2_out, not_3_out);
  and and_16 (and_16_out, In[2], In[1], In[0]);
  and and_17 (and_17_out, In[3], In[1]);
  and and_18 (and_18_out, In[3], In[2]);
  or or_1 (A, In[3], and_1_out, and_2_out, In[1]);
  or or_2 (B, not_2_out, and_3_out, and_4_out);
  or or_3 (C, In[2], not_3_out, In[0]);
  or or_4 (or_4_out, and_5_out, and_6_out, and_7_out, and_8_out, and_9_out);
  or or_5 (or_5_out, and_10_out, In[0], and_11_out);
  or or_6 (or_6_out, and_12_out, and_13_out, and_14_out);
  or or_7 (or_7_out, and_15_out, and_16_out, and_17_out, and_18_out);
  not not_5 (D, or_4_out);
  not not_6 (E, or_5_out);
  not not_7 (F, or_6_out);
  not not_8 (G, or_7_out);

  // Other names for the same wires on the sheet: _0 = A; _1 = B; _2 = C; _3 = D; _4 = E; _5 = F; _6 = G; d_t = In[0];
  //   c_t = In[1]; b_t = In[2]; a_t = In[3]
endmodule
