// Digital circuit 3_02.dig as structural Verilog
module _3_02 (
  input  [2:0] In,
  output [7:0] Z
);

  wire v0_t, v0_v1, v0_v1_t, v0_v1_v2, v0_v1_v2_t, v0_v1v2, v0_v1v2_t, v0_v2, v0v1, v0v1_t, v0v1_v2,
       v0v1_v2_t, v0v1v2, v0v1v2_t, v0v2, v0v2_t, v1_t, v1_v2, v1v2, v1v2_t, v2_t;

  and and_1 (v0v1v2, In[0], In[1], In[2]);
  and and_2 (v0v1v2_t, In[0], In[1], v2_t);
  and and_3 (v0v1_v2, In[0], v1_t, In[2]);
  and and_4 (v0v1_v2_t, In[0], v1_t, v2_t);
  and and_5 (v0_v1v2, v0_t, In[1], In[2]);
  and and_6 (v0_v1v2_t, v0_t, In[1], v2_t);
  and and_7 (v0_v1_v2, v0_t, v1_t, In[2]);
  and and_8 (v0_v1_v2_t, v0_t, v1_t, v2_t);
  and and_9 (Z[7], In[0], v0_t);
  or or_1 (Z[6], In[0], v0_t);
  or or_2 (Z[3], v0v2_t, v1_v2);
  or or_3 (Z[5], v1v2, v0_v1, v0_v2, v0v1_v2_t);
  or or_4 (Z[2], v0_v1_t, v1_v2, v1v2_t);
  or or_5 (Z[1], v0v1v2, v0_v1_v2, v0_v1v2_t);
  or or_6 (Z[0], v0_v1, v0v1_v2_t, v0_v1_v2);
  and and_10 (v0v1, In[0], In[1]);
  and and_11 (v0v2, In[0], In[2]);
  and and_12 (v0v1_t, In[0], v1_t);
  and and_13 (v0v2_t, In[0], v2_t);
  and and_14 (v0_v1_t, v0_t, v1_t);
  and and_15 (v1v2, In[1], In[2]);
  and and_16 (v1v2_t, In[1], v2_t);
  and and_17 (v1_v2, v1_t, In[2]);
  and and_18 (v0_v1, v0_t, In[1]);
  and and_19 (v0_v2, v0_t, In[2]);
  not not_1 (v0_t, In[0]);
  not not_2 (v1_t, In[1]);
  not not_3 (v2_t, In[2]);

  assign Z[4] = Z[7];

  // Other names for the same wires on the sheet: _0 = Z[7]; _1 = Z[6]; v0 = In[0]; v1 = In[1]; v2 = In[2]
endmodule
