// Digital circuit 3_04.dig as structural Verilog
module _3_04 (
  input  [6:0] In,
  output [6:0] Output
);

  wire e1, e2, e3, e4, e5, e6, e7, not_1_out, not_2_out, not_3_out, s1, s2, s3;

  xor xor_1 (s1, In[6], In[4], In[2], In[0]);
  xor xor_2 (s2, In[5], In[4], In[1], In[0]);
  xor xor_3 (s3, In[3], In[2], In[1], In[0]);
  not not_1 (not_1_out, s3);
  not not_2 (not_2_out, s2);
  not not_3 (not_3_out, s1);
  and and_1 (e1, not_1_out, not_2_out, s1);
  and and_2 (e2, not_1_out, s2, not_3_out);
  and and_3 (e3, not_1_out, s2, s1);
  and and_4 (e4, s3, not_2_out, not_3_out);
  and and_5 (e5, s3, not_2_out, s1);
  and and_6 (e6, s3, s2, not_3_out);
  and and_7 (e7, s3, s2, s1);
  xor xor_4 (Output[0], e7, In[0]);
  xor xor_5 (Output[1], e6, In[1]);
  xor xor_6 (Output[2], e5, In[2]);
  xor xor_7 (Output[3], e4, In[3]);
  xor xor_8 (Output[4], e3, In[4]);
  xor xor_9 (Output[5], e2, In[5]);
  xor xor_10 (Output[6], e1, In[6]);

  // Other names for the same wires on the sheet: i7 = In[0]; i6 = In[1]; i5 = In[2]; i4 = In[3]; i3 = In[4];
  //   i2 = In[5]; i1 = In[6]
endmodule
