// Digital circuit 7_01.dig as structural Verilog
module _7_01 (
  input  reset,
  input  clk,
  output C,
  output B,
  output A
);

  wire and_1_out, and_2_out, and_3_out, and_4_out, and_5_out, d_ff_1_nq, d_ff_2_nq, d_ff_3_nq, not_1_out,
       not_2_out, not_3_out, or_1_out;

  and and_1 (and_1_out, d_ff_3_nq, d_ff_1_nq);
  or or_1 (or_1_out, d_ff_2_nq, and_1_out);
  and and_2 (and_2_out, B, d_ff_1_nq);
  not not_1 (not_1_out, reset);
  not not_2 (not_2_out, reset);
  not not_3 (not_3_out, reset);
  and and_3 (and_3_out, not_1_out, A);
  and and_4 (and_4_out, not_2_out, or_1_out);
  and and_5 (and_5_out, not_3_out, and_2_out);
  D_FF d_ff_1 (.D(and_3_out), .C(clk), .Q(C), .nQ(d_ff_1_nq));
  D_FF d_ff_2 (.D(and_4_out), .C(clk), .Q(B), .nQ(d_ff_2_nq));
  D_FF d_ff_3 (.D(and_5_out), .C(clk), .Q(A), .nQ(d_ff_3_nq));
endmodule
