// Digital circuit 8_01.dig as structural Verilog
module _8_01 (
  input  [7:0] A,
  input  [7:0] B,
  input  start,
  input  clear,
  input  clk,
  output [7:0] \output ,
  output busy
);

  wire _00, _01, _10, _11, and_1_out, and_2_out, eq, gt, lt, multiplexer_1_out, multiplexer_2_out, not_2_out,
       or_1_out, or_2_out, q1, q2;
  wire [7:0] a_t, b_t, multiplexer_3_out, multiplexer_4_out, sub_1_s, sub_2_s;

  not not_1 (busy, _00);
  Multiplexer #(.Selector_Bits(2)) multiplexer_1 (
    .sel({q1, q2}), .in_0(start), .in_1(1'b1), .in_2(1'b1), .in_3(gt), .out(multiplexer_1_out));
  Multiplexer #(.Selector_Bits(2)) multiplexer_2 (
    .sel({q1, q2}), .in_0(start), .in_1(1'b1), .in_2(1'b1), .in_3(lt), .out(multiplexer_2_out));
  not not_2 (not_2_out, clear);
  and and_1 (and_1_out, not_2_out, multiplexer_1_out);
  and and_2 (and_2_out, not_2_out, multiplexer_2_out);
  Sub #(.Bits(8)) sub_1 (.a(a_t), .b(b_t), .c_i(1'b0), .s(sub_1_s));  // open: c_o
  or or_1 (or_1_out, _00, _10);
  Sub #(.Bits(8)) sub_2 (.a(b_t), .b(a_t), .c_i(1'b0), .s(sub_2_s));  // open: c_o
  or or_2 (or_2_out, _00, _01);
  D_FF d_ff_1 (.D(and_1_out), .C(clk), .Q(q1));  // open: nQ
  D_FF d_ff_2 (.D(and_2_out), .C(clk), .Q(q2));  // open: nQ
  Decoder #(.Selector_Bits(2)) decoder_1 (.sel({q1, q2}), .out_0(_00), .out_1(_01), .out_2(_10), .out_3(_11));
  Multiplexer #(.Bits(8)) multiplexer_3 (.sel(_10), .in_0(A), .in_1(sub_1_s), .out(multiplexer_3_out));
  Multiplexer #(.Bits(8)) multiplexer_4 (.sel(_01), .in_0(B), .in_1(sub_2_s), .out(multiplexer_4_out));
  Register #(.Bits(8)) register_1 (.D(multiplexer_3_out), .C(clk), .en(or_1_out), .Q(a_t));
  Register #(.Bits(8)) register_2 (.D(multiplexer_4_out), .C(clk), .en(or_2_out), .Q(b_t));
  Register #(.Bits(8)) register_3 (.D(a_t), .C(clk), .en(_11), .Q(\output ));
  Comparator #(.Bits(8)) comparator_1 (.a(a_t), .b(b_t), .gt(gt), .eq(eq), .lt(lt));

  // Other names for the same wires on the sheet: clr = clear
endmodule
